// Logisim project ADDER.circ as structural Verilog: 5 circuits, main circuit Full Adder
module Full_Adder (
  input  in_1,
  input  in_2,
  input  in_3,
  output out_4,
  output out_5
);

  wire and_1_out, and_2_out, xor_1_out;

  xor xor_1 (xor_1_out, in_1, in_2);
  and and_1 (and_1_out, in_3, xor_1_out);
  and and_2 (and_2_out, in_2, in_1);
  xor xor_2 (out_5, xor_1_out, in_3);
  or or_1 (out_4, and_1_out, and_2_out);
endmodule

module Half_Adder (
  input  in_1,
  input  in_2,
  output out_3,
  output out_4
);

  and and_1 (out_3, in_1, in_2);
  xor xor_1 (out_4, in_1, in_2);
endmodule

module TWOCOMP (
  input  [7:0] in_1,
  input  in_2,
  input  [7:0] in_3,
  output [7:0] out_4,
  output out_5
);

  wire full_adder_1_out_5, full_adder_2_out_4, full_adder_2_out_5, full_adder_3_out_4, full_adder_3_out_5,
       full_adder_5_out_4, full_adder_5_out_5, full_adder_6_out_4, full_adder_7_out_4, full_adder_7_out_5,
       full_adder_8_out_4, full_adder_8_out_5, full_adder_9_out_4, full_adder_10_out_4, full_adder_10_out_5,
       full_adder_11_out_4, full_adder_12_out_4, full_adder_13_out_4, full_adder_14_out_4,
       half_adder_1_out_3, half_adder_1_out_4, half_adder_2_out_3, multiplexer_1_out, multiplexer_2_out,
       multiplexer_3_out, multiplexer_4_out, multiplexer_5_out, multiplexer_6_out, multiplexer_7_out,
       multiplexer_8_out, not_1_out, not_2_out, not_3_out, not_4_out, not_5_out, not_6_out, not_7_out,
       not_8_out, not_9_out;

  Multiplexer multiplexer_1 (.in0(in_1[7]), .in1(full_adder_1_out_5), .out(multiplexer_1_out), .sel(in_2));  // open: en
  not not_1 (not_1_out, in_1[7]);
  not not_2 (not_2_out, in_1[6]);
  Full_Adder full_adder_1 (
    .in_1(full_adder_3_out_4), .in_2(not_1_out), .in_3(not_9_out), .out_5(full_adder_1_out_5));  // open: out_4
  Multiplexer multiplexer_2 (.in0(in_1[6]), .in1(full_adder_3_out_5), .out(multiplexer_2_out), .sel(in_2));  // open: en
  not not_3 (not_3_out, in_1[5]);
  Full_Adder full_adder_2 (
    .in_1(full_adder_5_out_4), .in_2(not_3_out), .in_3(not_9_out), .out_4(full_adder_2_out_4),
    .out_5(full_adder_2_out_5));
  Full_Adder full_adder_3 (
    .in_1(full_adder_2_out_4), .in_2(not_2_out), .in_3(not_9_out), .out_4(full_adder_3_out_4),
    .out_5(full_adder_3_out_5));
  Multiplexer multiplexer_3 (.in0(in_1[5]), .in1(full_adder_2_out_5), .out(multiplexer_3_out), .sel(in_2));  // open: en
  Full_Adder full_adder_4 (
    .in_1(full_adder_6_out_4), .in_2(in_3[7]), .in_3(multiplexer_1_out), .out_4(out_5), .out_5(out_4[7]));
  not not_4 (not_4_out, in_1[4]);
  not not_5 (not_5_out, in_1[3]);
  Full_Adder full_adder_5 (
    .in_1(full_adder_8_out_4), .in_2(not_4_out), .in_3(not_9_out), .out_4(full_adder_5_out_4),
    .out_5(full_adder_5_out_5));
  Multiplexer multiplexer_4 (.in0(in_1[3]), .in1(full_adder_8_out_5), .out(multiplexer_4_out), .sel(in_2));  // open: en
  Multiplexer multiplexer_5 (.in0(in_1[4]), .in1(full_adder_5_out_5), .out(multiplexer_5_out), .sel(in_2));  // open: en
  Full_Adder full_adder_6 (
    .in_1(full_adder_9_out_4), .in_2(in_3[6]), .in_3(multiplexer_2_out), .out_4(full_adder_6_out_4),
    .out_5(out_4[6]));
  not not_6 (not_6_out, in_1[2]);
  Full_Adder full_adder_7 (
    .in_1(full_adder_10_out_4), .in_2(not_6_out), .in_3(not_9_out), .out_4(full_adder_7_out_4),
    .out_5(full_adder_7_out_5));
  Full_Adder full_adder_8 (
    .in_1(full_adder_7_out_4), .in_2(not_5_out), .in_3(not_9_out), .out_4(full_adder_8_out_4),
    .out_5(full_adder_8_out_5));
  Multiplexer multiplexer_6 (.in0(in_1[2]), .in1(full_adder_7_out_5), .out(multiplexer_6_out), .sel(in_2));  // open: en
  Full_Adder full_adder_9 (
    .in_1(full_adder_12_out_4), .in_2(in_3[5]), .in_3(multiplexer_3_out), .out_4(full_adder_9_out_4),
    .out_5(out_4[5]));
  not not_7 (not_7_out, in_1[1]);
  not not_8 (not_8_out, in_1[0]);
  Full_Adder full_adder_10 (
    .in_1(half_adder_1_out_3), .in_2(not_7_out), .in_3(not_9_out), .out_4(full_adder_10_out_4),
    .out_5(full_adder_10_out_5));
  Multiplexer multiplexer_7 (
    .in0(in_1[1]), .in1(full_adder_10_out_5), .out(multiplexer_7_out), .sel(in_2));  // open: en
  Full_Adder full_adder_11 (
    .in_1(full_adder_13_out_4), .in_2(in_3[3]), .in_3(multiplexer_4_out), .out_4(full_adder_11_out_4),
    .out_5(out_4[3]));
  Full_Adder full_adder_12 (
    .in_1(full_adder_11_out_4), .in_2(in_3[4]), .in_3(multiplexer_5_out), .out_4(full_adder_12_out_4),
    .out_5(out_4[4]));
  not not_9 (not_9_out, 1'b1);
  Half_Adder half_adder_1 (.in_1(1'b1), .in_2(not_8_out), .out_3(half_adder_1_out_3), .out_4(half_adder_1_out_4));
  Multiplexer multiplexer_8 (.in0(in_1[0]), .in1(half_adder_1_out_4), .out(multiplexer_8_out), .sel(in_2));  // open: en
  Full_Adder full_adder_13 (
    .in_1(full_adder_14_out_4), .in_2(in_3[2]), .in_3(multiplexer_6_out), .out_4(full_adder_13_out_4),
    .out_5(out_4[2]));
  Full_Adder full_adder_14 (
    .in_1(half_adder_2_out_3), .in_2(in_3[1]), .in_3(multiplexer_7_out), .out_4(full_adder_14_out_4),
    .out_5(out_4[1]));
  Half_Adder half_adder_2 (.in_1(in_3[0]), .in_2(multiplexer_8_out), .out_3(half_adder_2_out_3), .out_4(out_4[0]));
endmodule

module ADDER (
  input  in_1,
  input  [7:0] in_2,
  input  [7:0] in_3,
  output out_4,
  output [7:0] out_5
);

  wire [7:0] adder_1_out, multiplexer_1_out, not_1_out;

  assign not_1_out = ~in_2;  // NOT_Gate not_1, 8 bits wide
  Multiplexer #(.width(8)) multiplexer_1 (
    .in0(in_2), .in1(adder_1_out), .out(multiplexer_1_out), .sel(in_1));  // open: en
  Adder adder_1 (.a(not_1_out), .b(8'h1), .out(adder_1_out));  // open: cin, cout
  Adder adder_2 (.a(in_3), .b(multiplexer_1_out), .out(out_5), .cout(out_4));  // open: cin
endmodule

module with_register (
  input  [7:0] in_1,
  input  in_2,
  input  in_3,
  input  in_4,
  input  in_5
);

  wire adder_1_out_4, clock_1_out;
  wire [7:0] adder_1_out_5, demultiplexer_1_out0, demultiplexer_1_out1, multiplexer_1_out, multiplexer_2_out,
       multiplexer_3_out, multiplexer_4_out, register_1_q, register_2_q, register_3_q, register_4_q;

  Multiplexer #(.width(8)) multiplexer_1 (
    .in0(in_1), .in1(adder_1_out_5), .out(multiplexer_1_out), .sel(in_4));  // open: en
  Clock clock_1 (.out(clock_1_out));
  Register register_1 (.D(multiplexer_1_out), .Q(register_1_q), .clk(clock_1_out));  // open: en, clr
  Multiplexer #(.width(8)) multiplexer_2 (
    .in0(in_1), .in1(register_1_q), .out(multiplexer_2_out), .sel(in_4));  // open: en
  Multiplexer #(.width(8)) multiplexer_3 (
    .in0(multiplexer_2_out), .in1(adder_1_out_5), .out(multiplexer_3_out), .sel(in_3));  // open: en
  Multiplexer #(.width(8)) multiplexer_4 (
    .in0(multiplexer_2_out), .in1(register_2_q), .out(multiplexer_4_out), .sel(in_3));  // open: en
  Register register_2 (.D(multiplexer_3_out), .Q(register_2_q), .clk(clock_1_out));  // open: en, clr
  Demultiplexer #(.width(8)) demultiplexer_1 (
    .out0(demultiplexer_1_out0), .out1(demultiplexer_1_out1), .in(multiplexer_4_out), .sel(in_2));  // open: en
  Register register_3 (.D(demultiplexer_1_out0), .Q(register_3_q), .clk(clock_1_out));  // open: en, clr
  Register register_4 (.D(demultiplexer_1_out1), .Q(register_4_q), .clk(clock_1_out));  // open: en, clr
  ADDER adder_1 (.in_1(in_5), .in_2(register_3_q), .in_3(register_4_q), .out_4(adder_1_out_4), .out_5(adder_1_out_5));
endmodule
