// Logisim project CPU-Modified-PC.circ as structural Verilog: 16 circuits, main circuit trying_counter
module main (
  input  [3:0] in_1,
  input  in_2,
  input  [7:0] in_3,
  input  in_4,
  input  [7:0] in_5,
  input  [7:0] in_6,
  input  in_7,
  input  in_8,
  output [7:0] out_9,
  output [7:0] out_10,
  output [7:0] out_11
);

  wire and_1_out, and_2_out, and_3_out, and_4_out, and_5_out, and_6_out, and_7_out, and_8_out, clock_1_out,
       clock_2_out, d_ff_1_q, main_1_out_11, main_2_out_2, main_2_out_3, main_2_out_4, main_2_out_5,
       main_2_out_6, main_2_out_7, main_2_out_8, main_3_out_2, main_3_out_3, main_3_out_4, main_3_out_5,
       main_3_out_6, main_3_out_7, main_3_out_8, main_4_out_2, main_4_out_3, main_4_out_4, main_4_out_5,
       main_4_out_6, main_4_out_7, main_4_out_8;
  wire [3:0] adder_1_out, multiplexer_1_out, register_1_q, yeah_1_out_21, yeah_1_out_22, yeah_1_out_23;
  wire [7:0] adder_2_out, mbr_1_out_5, RAM_out_5, register_2_q;

  _4BitCounter_main main_1 (
    .in_1(clock_1_out), .in_2(in_1), .in_3(in_2), .out_11(main_1_out_11));  // open: out_4, out_5, out_6, out_10, out_7, out_8, out_9
  Clock clock_1 (.out(clock_1_out));
  Multiplexer #(.width(4)) multiplexer_1 (
    .in0(4'b0000), .in1(4'b0001), .out(multiplexer_1_out), .sel(main_1_out_11));  // open: en
  Adder #(.width(4)) adder_1 (.a(multiplexer_1_out), .b(register_1_q), .out(adder_1_out));  // open: cin, cout
  MBR mbr_1 (.out_6(out_10), .in_1(in_6), .in_2(in_5), .in_3(in_7), .in_4(in_8), .out_5(mbr_1_out_5));
  Adder adder_2 (.a(register_2_q), .b(8'h7), .out(adder_2_out));  // open: cin, cout
  Register #(.width(4)) register_1 (.D(adder_1_out), .Q(register_1_q), .clk(clock_1_out));  // open: en, clr
  Register register_2 (.D(adder_2_out), .Q(register_2_q), .clk(clock_1_out));  // open: en, clr
  RAM RAM (.in_3(register_2_q), .in_1(in_4), .in_2(clock_1_out), .out_5(RAM_out_5), .in_4(register_1_q));
  _7_Segment_Display u_7_segment_display_1 (
    .g(main_2_out_2), .f(main_2_out_3), .a(main_2_out_4), .b(main_2_out_5), .e(main_2_out_8),
    .d(main_2_out_7), .c(main_2_out_6));  // open: dp
  Register register_3 (.D(RAM_out_5), .Q(out_9), .clk(clock_1_out));  // open: en, clr
  display_main main_2 (
    .in_1(yeah_1_out_23), .out_6(main_2_out_6), .out_7(main_2_out_7), .out_8(main_2_out_8),
    .out_2(main_2_out_2), .out_3(main_2_out_3), .out_4(main_2_out_4), .out_5(main_2_out_5));
  _7_Segment_Display u_7_segment_display_2 (
    .g(main_3_out_2), .f(main_3_out_3), .a(main_3_out_4), .b(main_3_out_5), .e(main_3_out_8),
    .d(main_3_out_7), .c(main_3_out_6));  // open: dp
  Yeah yeah_1 (
    .in_1(1'b0), .in_2(1'b0), .in_3(1'b0), .in_4(1'b0), .in_5(1'b0), .in_6(1'b0), .in_7(1'b0), .in_8(1'b0),
    .in_9(1'b0), .in_10(1'b0), .in_11(1'b0), .in_12(1'b0), .in_13(in_3[7]), .in_14(in_3[6]), .in_15(in_3[5]),
    .in_16(in_3[4]), .in_17(in_3[3]), .in_18(in_3[2]), .in_19(in_3[1]), .in_20(in_3[0]),
    .out_21(yeah_1_out_21), .out_22(yeah_1_out_22), .out_23(yeah_1_out_23));
  display_main main_3 (
    .in_1(yeah_1_out_22), .out_6(main_3_out_6), .out_7(main_3_out_7), .out_8(main_3_out_8),
    .out_2(main_3_out_2), .out_3(main_3_out_3), .out_4(main_3_out_4), .out_5(main_3_out_5));
  _7_Segment_Display u_7_segment_display_3 (
    .g(main_4_out_2), .f(main_4_out_3), .a(main_4_out_4), .b(main_4_out_5), .e(main_4_out_8),
    .d(main_4_out_7), .c(main_4_out_6));  // open: dp
  display_main main_4 (
    .in_1(yeah_1_out_21), .out_6(main_4_out_6), .out_7(main_4_out_7), .out_8(main_4_out_8),
    .out_2(main_4_out_2), .out_3(main_4_out_3), .out_4(main_4_out_4), .out_5(main_4_out_5));
  and and_1 (and_1_out, clock_2_out, clock_2_out);
  and and_2 (and_2_out, and_1_out, and_1_out);
  and and_3 (and_3_out, and_2_out, and_2_out);
  and and_4 (and_4_out, and_5_out, and_5_out);
  and and_5 (and_5_out, and_3_out, and_3_out);
  and and_6 (and_6_out, and_4_out, and_4_out);
  and and_7 (and_7_out, and_6_out, and_6_out);
  and and_8 (and_8_out, and_7_out, and_7_out);
  Clock clock_2 (.out(clock_2_out));
  D_Flip_Flop d_ff_1 (.clk(clock_2_out), .D(and_8_out), .Q(d_ff_1_q));  // open: Qn, preset, en, reset
endmodule

module ADD (
  input  [7:0] in_1,
  input  in_2,
  input  ITEM_5,
  input  ITEM_4,
  input  in_5,
  input  in_6,
  input  ITEM_2,
  input  in_8,
  input  in_9,
  input  in_10,
  output out_11
);

  wire and_1_out, and_2_out, and_3_out, and_4_out, clock_1_out, decoder_1_out0, decoder_1_out1,
       decoder_2_out0, decoder_2_out1;
  wire [7:0] adder_1_out_5, multiplexer_1_out, multiplexer_2_out, multiplexer_3_out, register_1_q,
       register_2_q, register_3_q, register_4_q, register_5_q;

  Multiplexer #(.width(8)) multiplexer_1 (
    .in0(in_1), .in1(register_5_q), .out(multiplexer_1_out), .sel(in_8));  // open: en
  Register register_1 (.D(multiplexer_1_out), .Q(register_1_q), .clk(and_1_out));  // open: en, clr
  and and_1 (and_1_out, decoder_1_out0, ITEM_5, clock_1_out);
  Decoder decoder_1 (.out0(decoder_1_out0), .out1(decoder_1_out1), .sel(ITEM_4));  // open: en
  Clock clock_1 (.out(clock_1_out));
  Register register_2 (.D(multiplexer_1_out), .Q(register_2_q), .clk(and_2_out));  // open: en, clr
  and and_2 (and_2_out, decoder_1_out1, ITEM_5, clock_1_out);
  Multiplexer #(.width(8)) multiplexer_2 (
    .in0(register_1_q), .in1(register_2_q), .out(multiplexer_2_out), .sel(in_5));  // open: en
  Multiplexer #(.width(8)) multiplexer_3 (
    .in0(multiplexer_1_out), .in1(multiplexer_2_out), .out(multiplexer_3_out), .sel(in_6));  // open: en
  Register register_3 (.D(multiplexer_3_out), .Q(register_3_q), .clk(and_3_out));  // open: en, clr
  and and_3 (and_3_out, clock_1_out, decoder_2_out0, decoder_2_out0);
  Decoder decoder_2 (.out0(decoder_2_out0), .out1(decoder_2_out1), .sel(ITEM_2));  // open: en
  Register register_4 (.D(multiplexer_3_out), .Q(register_4_q), .clk(and_4_out));  // open: en, clr
  and and_4 (and_4_out, clock_1_out, decoder_2_out1, decoder_2_out1);
  ADDER adder_1 (.in_1(in_2), .in_2(register_3_q), .in_3(register_4_q), .out_4(out_11), .out_5(adder_1_out_5));
  Register register_5 (.D(adder_1_out_5), .Q(register_5_q), .clk(clock_1_out));  // open: en, clr

  // Notes on the sheet:
  //   ITEM 1
  //   ITEM 3
  //   A-OUT
endmodule

// CONTROL UNIT
module CONTROL_UNIT (
  input  [7:0] in_1,
  input  in_2,
  output out_3,
  output out_4,
  output out_5,
  output out_6,
  output R1,
  output R2,
  output out_9,
  output out_10,
  output out_11,
  output out_12,
  output out_13,
  output out_14,
  output out_15,
  output out_16,
  output out_17,
  output out_18,
  output out_19,
  output out_20,
  output out_21,
  output out_22,
  output out_23,
  output out_24
);

  wire _00, _01, _1, _2, _3, _4, _8, _10, _11, ADD, ADD_out, and_1_out, and_4_out, and_5_out, and_6_out,
       and_7_out, and_8_out, and_9_out, and_10_out, and_11_out, and_12_out, and_13_out, and_14_out,
       and_23_out, and_24_out, and_25_out, and_27_out, ARG1, ARG2, B1, B2, decoder_1_out0, decoder_1_out1,
       delay_1_out_2, delay_2_out_2, delay_3_out_2, delay_6_out_2, delay_7_out_2, DEST, DONE, FIVE, GO, INP,
       INP_out, LOAD, not_1_out, not_2_out, not_3_out, not_4_out, not_5_out, not_6_out, not_7_out, not_8_out,
       not_9_out, not_10_out, not_11_out, not_12_out, not_13_out, not_14_out, not_15_out, not_16_out,
       not_17_out, not_18_out, not_19_out, not_20_out, not_21_out, not_22_out, not_23_out, or_1_out,
       or_2_out, or_3_out, or_4_out, or_6_out, or_7_out, or_8_out, or_9_out, or_11_out, or_12_out, or_13_out,
       or_15_out, or_16_out, or_17_out, or_18_out, or_20_out, or_22_out, PRT, PRT_out, SIX, STP, STP_out,
       SUB, SUB_out, SVN;
  wire [3:0] _1TK, _4TX, _5TX, adder_1_out, jmp, multiplexer_6_out, multiplexer_7_out, or_19_out;
  wire [7:0] multiplexer_3_out, multiplexer_5_out, multiplexer_8_out, multiplexer_9_out, or_23_out;

  DELAY delay_1 (.in_1(or_4_out), .out_2(delay_1_out_2));
  or or_1 (or_1_out, ARG1, DEST);
  and and_1 (and_1_out, or_1_out, or_2_out);
  or or_2 (or_2_out, ADD, SUB, INP, LOAD);
  D_Flip_Flop d_ff_1 (.clk(FIVE), .D(STP), .Q(DONE));  // open: Qn, preset, en, reset
  and and_2 (R1, decoder_1_out0, delay_1_out_2, in_2);
  Decoder decoder_1 (.out0(decoder_1_out0), .out1(decoder_1_out1), .sel(and_1_out));  // open: en
  and and_3 (R2, decoder_1_out1, delay_1_out_2, in_2);
  and and_4 (and_4_out, or_3_out, in_2, out_18);
  or or_3 (or_3_out, ADD, SUB);
  or or_4 (or_4_out, and_4_out, and_6_out, and_5_out);
  and and_5 (and_5_out, delay_2_out_2, INP);
  and and_6 (and_6_out, out_18, LOAD);
  buf or_5 (out_5, or_7_out);  // OR_Gate
  and and_7 (and_7_out, DEST, out_19);
  or or_6 (or_6_out, ARG1, B1);
  DELAY delay_2 (.in_1(SIX), .out_2(delay_2_out_2));
  or or_7 (or_7_out, and_7_out, and_12_out, and_8_out);
  and and_8 (and_8_out, or_8_out, out_6);
  or or_8 (or_8_out, and_9_out, and_11_out, and_10_out);
  and and_9 (and_9_out, FIVE, or_6_out);
  and and_10 (and_10_out, SIX, or_9_out);
  or or_9 (or_9_out, ARG2, B2);
  or or_10 (out_6, or_11_out, or_12_out, out_19);
  or or_11 (or_11_out, ADD, ADD);
  and and_11 (and_11_out, out_13, or_13_out);
  and and_12 (and_12_out, ARG1, PRT);
  or or_12 (or_12_out, out_3, PRT, out_4);
  or or_13 (or_13_out, B1, ARG1);
  not not_1 (not_1_out, out_9);
  and and_13 (and_13_out, ADD, not_1_out);
  not not_2 (not_2_out, out_9);
  and and_14 (and_14_out, SUB, not_2_out);
  not not_3 (not_3_out, multiplexer_5_out[2]);
  not not_4 (not_4_out, multiplexer_5_out[1]);
  not not_5 (not_5_out, multiplexer_5_out[0]);
  not not_6 (not_6_out, multiplexer_5_out[2]);
  not not_7 (not_7_out, multiplexer_5_out[3]);
  not not_8 (not_8_out, multiplexer_5_out[1]);
  and u_SUB (SUB_out, not_7_out, not_6_out, not_8_out, multiplexer_5_out[0]);
  and u_ADD (ADD_out, multiplexer_5_out[3], not_3_out, not_4_out, not_5_out);
  and and_15 (SUB, SUB_out, GO);
  and and_16 (ADD, ADD_out, GO);
  or or_14 (out_21, and_13_out, and_14_out);
  not not_9 (not_9_out, multiplexer_5_out[3]);
  not not_10 (not_10_out, multiplexer_5_out[3]);
  not not_11 (not_11_out, multiplexer_5_out[0]);
  and u_PRT (PRT_out, not_9_out, not_10_out, multiplexer_5_out[1], not_11_out);
  and and_17 (PRT, PRT_out, GO);
  Multiplexer #(.width(4)) multiplexer_1 (.in0(4'b0000), .in1(4'b0100), .out(_4TX), .sel(or_15_out));  // open: en
  or or_15 (or_15_out, SUB, ADD);
  Multiplexer #(.width(4)) multiplexer_2 (.in0(4'b0000), .in1(4'b0010), .out(_1TK), .sel(or_16_out));  // open: en
  or or_16 (or_16_out, PRT, STP, INP);
  not not_12 (not_12_out, multiplexer_3_out[4]);
  and and_18 (LOAD, not_12_out, GO, _01);
  not not_13 (not_13_out, multiplexer_5_out[3]);
  not not_14 (not_14_out, multiplexer_5_out[3]);
  not not_15 (not_15_out, multiplexer_5_out[2]);
  not not_16 (not_16_out, multiplexer_5_out[0]);
  not not_17 (not_17_out, multiplexer_5_out[1]);
  and u_STP (STP_out, not_14_out, not_15_out, not_17_out, not_16_out);
  and and_19 (STP, STP_out, _00, GO);
  and and_20 (out_19, multiplexer_3_out[4], GO, _01);
  not not_18 (not_18_out, multiplexer_5_out[1]);
  not not_19 (not_19_out, multiplexer_5_out[0]);
  and u_INP (INP_out, not_13_out, multiplexer_5_out[2], not_18_out, not_19_out);
  and and_21 (INP, INP_out, GO);
  and and_22 (GO, not_20_out, and_24_out);
  Multiplexer #(.width(8)) multiplexer_3 (
    .in0({8{1'b0}}), .in1(in_1), .out({multiplexer_3_out[7:6], DEST, multiplexer_3_out[4:0]}), .sel(_01));  // open: en
  or or_17 (or_17_out, ADD, SUB, out_3, out_4);
  DELAY delay_3 (.in_1(FIVE), .out_2(delay_3_out_2));
  and and_23 (and_23_out, or_17_out, delay_3_out_2);
  DELAY delay_4 (.in_1(and_23_out), .out_2(out_24));
  not not_20 (not_20_out, out_9);
  not not_21 (not_21_out, _1);
  not not_22 (not_22_out, _2);
  and and_24 (and_24_out, not_21_out, not_22_out, not_23_out);
  not not_23 (not_23_out, _3);
  Multiplexer #(.width(4)) multiplexer_4 (.in0(4'b0000), .in1(4'b0101), .out(_5TX), .sel(_01));  // open: en
  Multiplexer #(.width(8)) multiplexer_5 (
    .in0({8{1'b0}}), .in1(in_1), .out({multiplexer_5_out[7:6], ARG1, ARG2, multiplexer_5_out[3:0]}), .sel(_00));  // open: en
  or or_18 (or_18_out, ADD, SUB, out_3, out_4);
  and and_25 (and_25_out, or_18_out, delay_6_out_2);
  DELAY delay_5 (.in_1(and_25_out), .out_2(out_23));
  assign or_19_out = _4TX | _1TK | jmp | _5TX;  // OR_Gate or_19, 4 bits wide
  DELAY delay_6 (.in_1(SIX), .out_2(delay_6_out_2));
  // AND_Gate and_26 is placed but not wired
  Decoder #(.select(2)) decoder_2 (.out0(_00), .out1(_01), .out2(_10), .out3(_11), .sel(in_1[7:6]));  // open: en
  Adder #(.width(4)) adder_1 (.a(4'b0100), .b(or_19_out), .out(adder_1_out));  // open: cin, cout
  // _4BitCounter_main main_1: pin names not known; wires that end beside it: adder_1_out, DONE, _1, _2, _3, _4, out_14, out_15, out_16
  or or_20 (or_20_out, ADD, SUB, out_3, out_4);
  DELAY delay_7 (.in_1(SVN), .out_2(delay_7_out_2));
  and and_27 (and_27_out, or_20_out, delay_7_out_2);
  DELAY delay_8 (.in_1(and_27_out), .out_2(out_22));
  assign jmp = multiplexer_6_out | multiplexer_7_out;  // OR_Gate or_21, 4 bits wide
  Multiplexer #(.width(4)) multiplexer_6 (
    .in0(4'b0000), .in1(4'b0101), .out(multiplexer_6_out), .sel(_10));  // open: en
  Multiplexer #(.width(4)) multiplexer_7 (
    .in0(4'b0000), .in1(4'b0101), .out(multiplexer_7_out), .sel(_11));  // open: en
  Multiplexer #(.width(8)) multiplexer_8 (.in0({8{1'b0}}), .in1(in_1), .out(multiplexer_8_out), .sel(_10));  // open: en
  and and_28 (out_3, _10, GO);
  Multiplexer #(.width(8)) multiplexer_9 (.in0({8{1'b0}}), .in1(in_1), .out(multiplexer_9_out), .sel(_11));  // open: en
  or or_22 (or_22_out, out_16, _8);
  and and_29 (out_17, out_19, or_22_out);
  and and_30 (out_4, _11, GO);
  assign {or_23_out[7:6], B1, B2, or_23_out[3:0]} = multiplexer_8_out | multiplexer_9_out;  // OR_Gate or_23, 8 bits wide
  // AND_Gate and_31 is placed but not wired

  // Other names for the same wires on the sheet: _5 = out_14; _6 = out_15; _7 = out_16; _9 = out_20; BEQ = out_3;
  //   BNQ = out_4; CLK = in_2; EGT = out_18; FOUR = out_13; INSTR[7:0] = in_1; ONE = out_10; STORE = out_19;
  //   THREE = out_12; TWO = out_11; ZERO = out_9

  // Notes on the sheet:
  //   ITEM 4
  //   Choosing register MUX 4
  //   Puts value of chosen register to CPU bus - MUX 5
  //   Store in Register from A-Out (set mux to 1)
  //   ADDER PART
  //   Save to Left of ALU
  //   Save to Right of ALU
  //   save to A-Out
  //   MASTER_COUNTER
  //   Read mode of MBR
  //   Read/Write of RAM
endmodule

module trying_counter (
  input  in_1,
  input  in_2,
  input  ITEM_2,
  input  in_4,
  input  [7:0] in_5,
  input  [3:0] in_6,
  output out_7,
  output [7:0] out_8
);

  wire _7, _8, ADD, and_1_out, and_2_out, and_5_out, and_6_out, and_7_out, and_8_out, and_9_out, and_10_out,
       and_11_out, and_12_out, and_13_out, and_14_out, ARG1, ARG2, CLK, decoder_1_out0, decoder_1_out1,
       delay_1_out_2, delay_2_out_2, delay_3_out_2, delay_4_out_2, EGT, FIVE, FOUR, LOAD, not_1_out,
       not_2_out, not_3_out, not_4_out, ONE, or_2_out, SIX, SVN, THREE, TWO, ZERO;
  wire [3:0] adder_1_out, main_1_p1, mar_1_out_3, multiplexer_1_out, multiplexer_2_out, or_1_out,
       register_1_q;
  wire [7:0] adder_3_out_5, multiplexer_3_out, multiplexer_4_out, multiplexer_5_out, n8_bit_register_1_out_3,
       n8_bit_register_2_out_3, n8_bit_register_3_out_3, register_2_q, register_3_q, register_4_q,
       register_5_q;

  Adder #(.width(4)) adder_1 (.a(4'b0001), .b(register_1_q), .out(adder_1_out));  // open: cin, cout
  Register #(.width(4)) register_1 (.Q(register_1_q), .clk(delay_1_out_2));  // open: D, en, clr
  DELAY delay_1 (.in_1(TWO), .out_2(delay_1_out_2));
  // _4BitCounter_main main_1: pin names not known; wires that end beside it: main_1_p1, in_1, _7
  assign or_1_out = multiplexer_2_out | multiplexer_1_out;  // OR_Gate or_1, 4 bits wide
  Multiplexer #(.width(4)) multiplexer_1 (
    .in0(4'b0000), .in1(4'b0100), .out(multiplexer_1_out), .sel(and_1_out));  // open: en
  not not_1 (not_1_out, ZERO);
  Adder #(.width(4)) adder_2 (.a(4'b0100), .b(or_1_out), .out(main_1_p1));  // open: cin, cout
  RAM ram_1 (.in_3(in_5), .in_1(in_4), .in_2(CLK), .out_5(out_8), .in_4(mar_1_out_3));
  not not_2 (not_2_out, register_3_q[6]);
  not not_3 (not_3_out, register_3_q[7]);
  and and_1 (and_1_out, not_3_out, not_2_out);
  and and_2 (and_2_out, not_1_out, and_1_out);
  buf and_3 (ADD, and_2_out);  // AND_Gate
  and and_4 (LOAD, register_3_q[7], not_4_out);
  Multiplexer #(.width(4)) multiplexer_2 (
    .in0(4'b0000), .in1(4'b0100), .out(multiplexer_2_out), .sel(LOAD));  // open: en
  MAR mar_1 (.in_1(register_1_q), .in_2(ONE), .out_3(mar_1_out_3));
  not not_4 (not_4_out, register_3_q[6]);
  Register register_2 (.D(out_8), .Q(register_2_q), .clk(THREE));  // open: en, clr
  Register register_3 (
    .D(register_2_q), .Q({register_3_q[7:6], ARG1, ARG2, register_3_q[3:0]}), .clk(FOUR));  // open: en, clr
  Multiplexer #(.width(8)) multiplexer_3 (
    .in0({8{1'b0}}), .in1(register_5_q), .out(multiplexer_3_out), .sel(_8));  // open: en
  DELAY delay_2 (.in_1(and_5_out), .out_2(delay_2_out_2));
  and and_5 (and_5_out, EGT, ADD, CLK);
  _8_bit_register u_8_bit_register_1 (.in_1(multiplexer_3_out), .in_2(and_6_out), .out_3(n8_bit_register_1_out_3));
  and and_6 (and_6_out, decoder_1_out0, delay_2_out_2, CLK);
  Decoder decoder_1 (.out0(decoder_1_out0), .out1(decoder_1_out1), .sel(and_7_out));  // open: en
  Clock clock_1 (.out(CLK));
  and and_7 (and_7_out, ARG1, ADD);
  Register register_4 (.D(multiplexer_3_out), .Q(register_4_q), .clk(and_8_out));  // open: en, clr
  and and_8 (and_8_out, decoder_1_out1, delay_2_out_2, CLK);
  and and_9 (and_9_out, FIVE, ARG1);
  Multiplexer #(.width(8)) multiplexer_4 (
    .in0(n8_bit_register_1_out_3), .in1(register_4_q), .out(multiplexer_4_out), .sel(or_2_out));  // open: en
  or or_2 (or_2_out, and_9_out, and_11_out, and_10_out);
  and and_10 (and_10_out, SIX, ARG2);
  Multiplexer #(.width(8)) multiplexer_5 (
    .in0(multiplexer_3_out), .in1(multiplexer_4_out), .out(multiplexer_5_out), .sel(ADD));  // open: en
  and and_11 (and_11_out, FOUR, ARG1);
  _8_bit_register u_8_bit_register_2 (.in_1(multiplexer_5_out), .in_2(and_12_out), .out_3(n8_bit_register_2_out_3));
  and and_12 (and_12_out, delay_3_out_2, FIVE);
  DELAY delay_3 (.in_1(CLK), .out_2(delay_3_out_2));
  and and_13 (and_13_out, delay_4_out_2, SIX);
  DELAY delay_4 (.in_1(CLK), .out_2(delay_4_out_2));
  ADDER adder_3 (
    .in_1(in_2), .in_2(n8_bit_register_2_out_3), .in_3(n8_bit_register_3_out_3), .out_4(out_7),
    .out_5(adder_3_out_5));
  _8_bit_register u_8_bit_register_3 (.in_1(multiplexer_5_out), .in_2(and_13_out), .out_3(n8_bit_register_3_out_3));
  Register register_5 (.D(adder_3_out_5), .Q(register_5_q), .clk(and_14_out));  // open: en, clr
  and and_14 (and_14_out, CLK, SVN);
  T_Flip_Flop t_ff_1 (.clk(and_14_out), .T(ADD));  // open: Q, Qn, preset, reset, en
  // NOT_Gate not_5 is placed but not wired

  // Notes on the sheet:
  //   NOTE: ADD AND GATE IN TIMER
  //   IDEA: SEPARATE RAM INTO DATA AND INSTRUCTION FIELDS
  //   ITEM 4
  //   ITEM 1
  //   ITEM 3
  //   A-OUT
endmodule

module DELAY (
  input  in_1,
  output out_2
);

  wire and_1_out, and_2_out, and_3_out, and_4_out, and_5_out, and_6_out, and_7_out, and_8_out, and_9_out,
       and_10_out, and_11_out, and_12_out, and_13_out, and_14_out, and_15_out;

  and and_1 (and_1_out, in_1, in_1);
  and and_2 (and_2_out, and_3_out, and_3_out);
  and and_3 (and_3_out, and_1_out, and_1_out);
  and and_4 (and_4_out, and_2_out, and_2_out);
  and and_5 (and_5_out, and_4_out, and_4_out);
  and and_6 (and_6_out, and_5_out, and_5_out);
  and and_7 (and_7_out, and_6_out, and_6_out);
  and and_8 (and_8_out, and_7_out, and_7_out);
  and and_9 (and_9_out, and_8_out, and_8_out);
  and and_10 (and_10_out, and_9_out, and_9_out);
  and and_11 (and_11_out, and_10_out, and_10_out);
  and and_12 (and_12_out, and_11_out, and_11_out);
  and and_13 (and_13_out, and_12_out, and_12_out);
  and and_14 (and_14_out, and_13_out, and_13_out);
  and and_15 (and_15_out, and_14_out, and_14_out);
  and and_16 (out_2, and_15_out, and_15_out);
endmodule

module _8_bit_register (
  input  [7:0] in_1,
  input  in_2,
  output [7:0] out_3
);

  D_Flip_Flop d_ff_1 (.clk(in_2), .D(in_1[7]), .Q(out_3[7]));  // open: Qn, preset, en, reset
  D_Flip_Flop d_ff_2 (.clk(in_2), .D(in_1[6]), .Q(out_3[6]));  // open: Qn, preset, en, reset
  D_Flip_Flop d_ff_3 (.clk(in_2), .D(in_1[5]), .Q(out_3[5]));  // open: Qn, preset, en, reset
  D_Flip_Flop d_ff_4 (.clk(in_2), .D(in_1[4]), .Q(out_3[4]));  // open: Qn, preset, en, reset
  D_Flip_Flop d_ff_5 (.clk(in_2), .D(in_1[3]), .Q(out_3[3]));  // open: Qn, preset, en, reset
  D_Flip_Flop d_ff_6 (.clk(in_2), .D(in_1[2]), .Q(out_3[2]));  // open: Qn, preset, en, reset
  D_Flip_Flop d_ff_7 (.clk(in_2), .D(in_1[1]), .Q(out_3[1]));  // open: Qn, preset, en, reset
  D_Flip_Flop d_ff_8 (.clk(in_2), .D(in_1[0]), .Q(out_3[0]));  // open: Qn, preset, en, reset
endmodule

module BOARD (
  input  in_1,
  input  in_2,
  input  in_3,
  input  in_4,
  input  in_5,
  input  in_6,
  input  in_7,
  input  in_8,
  input  in_9,
  input  in_10,
  input  MUX_7,
  input  in_12,
  input  ITEM_2,
  output [3:0] out_14,
  output out_15
);

  wire _0FLAG, and_1_out, and_2_out, AOUT, BEQ, BNQ, CLK, control_unit_1_out_14, control_unit_1_out_16,
       control_unit_1_out_20, delay_1_out_2, delay_2_out_2, delay_3_out_2, delay_4_out_2, delay_5_out_2, EGT,
       FOUR, GPREG1, GPREG2, INP, LEFT, main_1_out_2, main_1_out_3, main_1_out_4, main_1_out_5, main_1_out_6,
       main_1_out_7, main_1_out_8, main_2_out_2, main_2_out_3, main_2_out_4, main_2_out_5, main_2_out_6,
       main_2_out_7, main_2_out_8, main_3_out_2, main_3_out_3, main_3_out_4, main_3_out_5, main_3_out_6,
       main_3_out_7, main_3_out_8, MBRCLK, MBRMODE, MUX3, MUX4, MUX5, MUX6, not_1_out, not_2_out, not_3_out,
       not_4_out, not_5_out, not_6_out, not_7_out, not_8_out, not_9_out, ONE, or_1_out, or_2_out, or_3_out,
       PRT, RIGHT, SAVEMAR, SIX, SUB, THREE, TWO, WRITERAM, ZERO;
  wire [3:0] adder_1_out, ADDRESS, mar_1_out_3, multiplexer_5_out, multiplexer_6_out, multiplexer_7_out,
       multiplexer_9_out, n8to4_1_out_2, yeah_1_out_21, yeah_1_out_22, yeah_1_out_23;
  wire [7:0] adder_2_out_5, keypad_1_out_11, L_out_3, MBR_out_5, MBR_out_6, multiplexer_1_out,
       multiplexer_2_out, multiplexer_3_out, multiplexer_4_out, multiplexer_8_out, multiplexer_10_out,
       n8_bit_register_1_out_3, n8_bit_register_2_out_3, n8_bit_register_3_out_3, n8_bit_register_4_out_3,
       n8_bit_register_5_out_3, R_out_3, ram_1_out_5;

  _7_Segment_Display u_7_segment_display_1 (
    .g(main_1_out_2), .f(main_1_out_3), .a(main_1_out_4), .b(main_1_out_5), .e(main_1_out_8),
    .d(main_1_out_7), .c(main_1_out_6));  // open: dp
  DELAY delay_1 (.in_1(CLK), .out_2(delay_1_out_2));
  display_main main_1 (
    .in_1(yeah_1_out_23), .out_6(main_1_out_6), .out_7(main_1_out_7), .out_8(main_1_out_8),
    .out_2(main_1_out_2), .out_3(main_1_out_3), .out_4(main_1_out_4), .out_5(main_1_out_5));
  _7_Segment_Display u_7_segment_display_2 (
    .g(main_2_out_2), .f(main_2_out_3), .a(main_2_out_4), .b(main_2_out_5), .e(main_2_out_8),
    .d(main_2_out_7), .c(main_2_out_6));  // open: dp
  Keypad keypad_1 (
    .in_9(in_1), .in_7(in_2), .in_10(in_3), .in_8(in_4), .in_5(in_5), .in_3(in_6), .in_6(in_7), .in_4(in_8),
    .in_2(in_9), .in_1(in_10), .out_11(keypad_1_out_11));
  RAM ram_1 (
    .in_3(multiplexer_1_out), .in_1(WRITERAM), .in_2(delay_1_out_2), .out_5(ram_1_out_5),
    .in_4(multiplexer_7_out));
  DELAY delay_2 (.in_1(delay_3_out_2), .out_2(delay_2_out_2));
  DELAY delay_3 (.in_1(PRT), .out_2(delay_3_out_2));
  _8_bit_register u_8_bit_register_1 (.in_1(multiplexer_3_out), .in_2(delay_2_out_2), .out_3(n8_bit_register_1_out_3));
  display_main main_2 (
    .in_1(yeah_1_out_22), .out_6(main_2_out_6), .out_7(main_2_out_7), .out_8(main_2_out_8),
    .out_2(main_2_out_2), .out_3(main_2_out_3), .out_4(main_2_out_4), .out_5(main_2_out_5));
  Multiplexer #(.width(8)) multiplexer_1 (
    .in0(keypad_1_out_11), .in1(MBR_out_6), .out(multiplexer_1_out), .sel(WRITERAM));  // open: en
  Multiplexer #(.width(8)) multiplexer_2 (
    .in0(ram_1_out_5), .in1(multiplexer_1_out), .out(multiplexer_2_out), .sel(INP));  // open: en
  Multiplexer #(.width(8)) multiplexer_3 (
    .in0(multiplexer_2_out), .in1(multiplexer_10_out), .out(multiplexer_3_out), .sel(PRT));  // open: en
  Yeah yeah_1 (
    .in_1(1'b0), .in_2(1'b0), .in_3(1'b0), .in_4(1'b0), .in_5(1'b0), .in_6(1'b0), .in_7(1'b0), .in_8(1'b0),
    .in_9(1'b0), .in_10(1'b0), .in_11(1'b0), .in_12(1'b0), .in_13(n8_bit_register_1_out_3[7]),
    .in_14(n8_bit_register_1_out_3[6]), .in_15(n8_bit_register_1_out_3[5]),
    .in_16(n8_bit_register_1_out_3[4]), .in_17(n8_bit_register_1_out_3[3]),
    .in_18(n8_bit_register_1_out_3[2]), .in_19(n8_bit_register_1_out_3[1]),
    .in_20(n8_bit_register_1_out_3[0]), .out_21(yeah_1_out_21), .out_22(yeah_1_out_22), .out_23(yeah_1_out_23));
  _7_Segment_Display u_7_segment_display_3 (
    .g(main_3_out_2), .f(main_3_out_3), .a(main_3_out_4), .b(main_3_out_5), .e(main_3_out_8),
    .d(main_3_out_7), .c(main_3_out_6));  // open: dp
  display_main main_3 (
    .in_1(yeah_1_out_21), .out_6(main_3_out_6), .out_7(main_3_out_7), .out_8(main_3_out_8),
    .out_2(main_3_out_2), .out_3(main_3_out_3), .out_4(main_3_out_4), .out_5(main_3_out_5));
  Multiplexer #(.width(8)) multiplexer_4 (
    .in0(MBR_out_5), .in1(n8_bit_register_4_out_3), .out(multiplexer_4_out), .sel(MUX3));  // open: en
  MBR MBR (
    .out_6(MBR_out_6), .in_1(multiplexer_2_out), .in_2(multiplexer_10_out), .in_3(MBRMODE), .in_4(MBRCLK),
    .out_5(MBR_out_5));
  Multiplexer #(.width(4)) multiplexer_5 (
    .in0(ADDRESS), .in1(n8to4_1_out_2), .out(multiplexer_5_out), .sel(in_12));  // open: en
  _8to4 u_8to4_1 (.in_1(multiplexer_4_out), .out_2(n8to4_1_out_2));
  Multiplexer #(.width(4)) multiplexer_6 (
    .in0(out_14), .in1(multiplexer_5_out), .out(multiplexer_6_out), .sel(MUX6));  // open: en
  MAR mar_1 (.in_1(multiplexer_6_out), .in_2(SAVEMAR), .out_3(mar_1_out_3));
  Multiplexer #(.width(4)) multiplexer_7 (.in0(mar_1_out_3), .out(multiplexer_7_out), .sel(MUX_7));  // open: in1, en
  _8_bit_register u_8_bit_register_2 (.in_1(multiplexer_4_out), .in_2(GPREG1), .out_3(n8_bit_register_2_out_3));
  _8_bit_register u_8_bit_register_3 (.in_1(multiplexer_4_out), .in_2(GPREG2), .out_3(n8_bit_register_3_out_3));
  Multiplexer #(.width(8)) multiplexer_8 (
    .in0(n8_bit_register_2_out_3), .in1(n8_bit_register_3_out_3), .out(multiplexer_8_out), .sel(MUX4));  // open: en
  Adder #(.width(4)) adder_1 (.a(4'b0001), .b(out_14), .out(adder_1_out));  // open: cin, cout
  or or_1 (or_1_out, BEQ, BNQ);
  Multiplexer #(.width(4)) multiplexer_9 (
    .in0(adder_1_out), .in1(ADDRESS), .out(multiplexer_9_out), .sel(or_1_out));  // open: en
  not not_1 (not_1_out, _0FLAG);
  Multiplexer #(.width(8)) multiplexer_10 (
    .in0(multiplexer_4_out), .in1(multiplexer_8_out), .out(multiplexer_10_out), .sel(MUX5));  // open: en
  PC pc_1 (.in_1(multiplexer_9_out), .in_2(delay_4_out_2), .out_3(out_14));
  DELAY delay_4 (.in_1(or_2_out), .out_2(delay_4_out_2));
  or or_2 (or_2_out, TWO, and_2_out, and_1_out);
  and and_1 (and_1_out, _0FLAG, EGT, BEQ);
  and and_2 (and_2_out, not_1_out, EGT, BNQ);
  _8_bit_register R (.in_1(multiplexer_10_out), .in_2(LEFT), .out_3(R_out_3));
  ADDER adder_2 (.in_1(or_3_out), .in_2(L_out_3), .in_3(R_out_3), .out_4(out_15), .out_5(adder_2_out_5));
  Clock clock_1 (.out(CLK));
  _8_bit_register L (.in_1(multiplexer_10_out), .in_2(delay_5_out_2), .out_3(L_out_3));
  DELAY delay_5 (.in_1(RIGHT), .out_2(delay_5_out_2));
  or or_3 (or_3_out, BNQ, SUB, BEQ);
  _8_bit_register u_8_bit_register_4 (.in_1(adder_2_out_5), .in_2(AOUT), .out_3(n8_bit_register_4_out_3));
  not not_2 (not_2_out, n8_bit_register_4_out_3[0]);
  not not_3 (not_3_out, n8_bit_register_4_out_3[1]);
  not not_4 (not_4_out, n8_bit_register_4_out_3[2]);
  not not_5 (not_5_out, n8_bit_register_4_out_3[3]);
  not not_6 (not_6_out, n8_bit_register_4_out_3[4]);
  not not_7 (not_7_out, n8_bit_register_4_out_3[5]);
  not not_8 (not_8_out, n8_bit_register_4_out_3[6]);
  not not_9 (not_9_out, n8_bit_register_4_out_3[7]);
  _8_bit_register u_8_bit_register_5 (.in_1(MBR_out_5), .in_2(FOUR), .out_3(n8_bit_register_5_out_3));
  CONTROL_UNIT control_unit_1 (
    .R1(GPREG1), .R2(GPREG2), .out_5(MUX4), .out_6(MUX5), .in_2(CLK), .in_1(n8_bit_register_5_out_3),
    .out_3(BEQ), .out_4(BNQ), .out_21(MUX3), .out_24(LEFT), .out_23(RIGHT), .out_22(AOUT), .out_19(MBRMODE),
    .out_17(WRITERAM), .out_9(ZERO), .out_10(ONE), .out_11(TWO), .out_12(THREE), .out_13(FOUR),
    .out_14(control_unit_1_out_14), .out_15(SIX), .out_16(control_unit_1_out_16), .out_18(EGT),
    .out_20(control_unit_1_out_20));
  and and_3 (_0FLAG, not_2_out, not_3_out, not_4_out, not_5_out, not_6_out, not_7_out, not_8_out, not_9_out);
  _8to4 u_8to4_2 (.in_1(n8_bit_register_5_out_3), .out_2(ADDRESS));
  CONTROL_UNIT_2 CONTROL_UNIT_2 (
    .in_2(CLK), .in_1(n8_bit_register_5_out_3), .MUX_6(MUX6), .out_14(MBRCLK), .out_15(PRT), .out_16(INP),
    .MAR(SAVEMAR), .out_18(SUB));  // open: out_3, out_4, out_5, out_6, out_7, out_8, out_9, out_10, out_11, out_12
  // NOT_Gate not_10 is placed but not wired

  // Notes on the sheet:
  //   When storing from MAR to AR, make long delay
  //   RAM mode
  //   Toggled when writing to RAM
  //   MUX 1
  //   SYSTEM BUS
  //   MUX 2
  //   MUX 3
  //   1 for writing from reg to MBR
  //   MBR r/w mode
  //   CPU BUS
  //   GP Registers
  //   MUX 6
  //   Toggled when AR <- MAR
  //   MUX 4
  //   MUX 5
  //   A-OUT
endmodule

module MBR (
  input  [7:0] in_1,
  input  [7:0] in_2,
  input  in_3,
  input  in_4,
  output [7:0] out_5,
  output [7:0] out_6
);

  wire [7:0] d_ff_8_q, multiplexer_1_out;

  Multiplexer #(.width(8)) multiplexer_1 (.in0(in_1), .in1(in_2), .out(multiplexer_1_out), .sel(in_3));  // open: en
  D_Flip_Flop d_ff_1 (.clk(in_4), .D(multiplexer_1_out[7]), .Q(d_ff_8_q[7]));  // open: Qn, preset, en, reset
  D_Flip_Flop d_ff_2 (.clk(in_4), .D(multiplexer_1_out[6]), .Q(d_ff_8_q[6]));  // open: Qn, preset, en, reset
  D_Flip_Flop d_ff_3 (.clk(in_4), .D(multiplexer_1_out[5]), .Q(d_ff_8_q[5]));  // open: Qn, preset, en, reset
  D_Flip_Flop d_ff_4 (.clk(in_4), .D(multiplexer_1_out[4]), .Q(d_ff_8_q[4]));  // open: Qn, preset, en, reset
  D_Flip_Flop d_ff_5 (.clk(in_4), .D(multiplexer_1_out[3]), .Q(d_ff_8_q[3]));  // open: Qn, preset, en, reset
  D_Flip_Flop d_ff_6 (.clk(in_4), .D(multiplexer_1_out[2]), .Q(d_ff_8_q[2]));  // open: Qn, preset, en, reset
  Demultiplexer #(.width(8)) demultiplexer_1 (.out0(out_5), .out1(out_6), .in(d_ff_8_q), .sel(in_3));  // open: en
  D_Flip_Flop d_ff_7 (.clk(in_4), .D(multiplexer_1_out[1]), .Q(d_ff_8_q[1]));  // open: Qn, preset, en, reset
  D_Flip_Flop d_ff_8 (.clk(in_4), .D(multiplexer_1_out[0]), .Q(d_ff_8_q[0]));  // open: Qn, preset, en, reset
endmodule

module MAR (
  input  [3:0] in_1,
  input  in_2,
  output [3:0] out_3
);

  D_Flip_Flop d_ff_1 (.clk(in_2), .D(in_1[3]), .Q(out_3[3]));  // open: Qn, preset, en, reset
  D_Flip_Flop d_ff_2 (.clk(in_2), .D(in_1[2]), .Q(out_3[2]));  // open: Qn, preset, en, reset
  D_Flip_Flop d_ff_3 (.clk(in_2), .D(in_1[1]), .Q(out_3[1]));  // open: Qn, preset, en, reset
  D_Flip_Flop d_ff_4 (.clk(in_2), .D(in_1[0]), .Q(out_3[0]));  // open: Qn, preset, en, reset
endmodule

module _8to4 (
  input  [7:0] in_1,
  output [3:0] out_2
);


  assign out_2 = in_1[3:0];
endmodule

module _4to8 (
  input  [3:0] in_1,
  output [7:0] out_2
);


  assign out_2 = {4'b0000, in_1};
endmodule

module PC (
  input  [3:0] in_1,
  input  in_2,
  output [3:0] out_3
);

  D_Flip_Flop d_ff_1 (.clk(in_2), .D(in_1[3]), .Q(out_3[3]));  // open: Qn, preset, en, reset
  D_Flip_Flop d_ff_2 (.clk(in_2), .D(in_1[2]), .Q(out_3[2]));  // open: Qn, preset, en, reset
  D_Flip_Flop d_ff_3 (.clk(in_2), .D(in_1[1]), .Q(out_3[1]));  // open: Qn, preset, en, reset
  D_Flip_Flop d_ff_4 (.clk(in_2), .D(in_1[0]), .Q(out_3[0]));  // open: Qn, preset, en, reset
endmodule

module LOAD (
  input  in_1,
  input  in_2,
  input  ITEM_2,
  input  [3:0] in_4,
  output out_5,
  output [7:0] out_6
);

  wire _6, _7, _8, ADD, and_1_out, and_2_out, and_4_out, and_6_out, and_7_out, and_8_out, and_9_out,
       and_10_out, and_11_out, and_12_out, and_13_out, and_14_out, and_15_out, and_16_out, and_17_out,
       and_18_out, ARG1, ARG2, CLK, decoder_1_out0, decoder_1_out1, delay_1_out_2, delay_2_out_2,
       delay_3_out_2, delay_4_out_2, delay_5_out_2, delay_6_out_2, delay_7_out_2, delay_8_out_2,
       delay_9_out_2, EGT, FIVE, FOUR, not_1_out, not_2_out, not_3_out, not_4_out, ONE, or_2_out, or_3_out,
       or_4_out, or_5_out, or_6_out, SIX, STORE, SVN, THREE, TWO, ZERO;
  wire [3:0] adder_2_out, address, main_1_p1, mar_1_out_3, multiplexer_1_out, multiplexer_2_out,
       multiplexer_3_out, or_1_out, register_2_q;
  wire [7:0] adder_3_out_5, multiplexer_4_out, multiplexer_5_out, multiplexer_6_out, n8_bit_register_1_out_3,
       n8_bit_register_2_out_3, n8_bit_register_3_out_3, register_1_q, register_3_q, register_5_q,
       register_6_q;
  wire [7:6] register_4_q;

  // _4BitCounter_main main_1: pin names not known; wires that end beside it: main_1_p1, in_1, _6, _7
  assign or_1_out = multiplexer_3_out | multiplexer_1_out;  // OR_Gate or_1, 4 bits wide
  Multiplexer #(.width(4)) multiplexer_1 (
    .in0(4'b0000), .in1(4'b0100), .out(multiplexer_1_out), .sel(and_2_out));  // open: en
  Register register_1 (.D(multiplexer_6_out), .Q(register_1_q), .clk(SIX));  // open: en, clr
  Adder #(.width(4)) adder_1 (.a(4'b0100), .b(or_1_out), .out(main_1_p1));  // open: cin, cout
  Adder #(.width(4)) adder_2 (.a(4'b0001), .b(register_2_q), .out(adder_2_out));  // open: cin, cout
  or or_2 (or_2_out, _7, _8);
  and and_1 (and_1_out, STORE, or_2_out);
  DELAY delay_1 (.in_1(CLK), .out_2(delay_1_out_2));
  RAM ram_1 (.in_3(register_1_q), .in_1(and_1_out), .in_2(delay_1_out_2), .out_5(out_6), .in_4(mar_1_out_3));
  not not_1 (not_1_out, register_4_q[6]);
  not not_2 (not_2_out, register_4_q[7]);
  and and_2 (and_2_out, not_2_out, not_1_out);
  buf and_3 (ADD, and_2_out);  // AND_Gate
  Register #(.width(4)) register_2 (.D(adder_2_out), .Q(register_2_q), .clk(delay_2_out_2));  // open: en, clr
  DELAY delay_2 (.in_1(TWO), .out_2(delay_2_out_2));
  Multiplexer #(.width(4)) multiplexer_2 (
    .in0(register_2_q), .in1(address), .out(multiplexer_2_out), .sel(and_4_out));  // open: en
  and and_4 (and_4_out, STORE, not_3_out);
  not not_3 (not_3_out, ZERO);
  Multiplexer #(.width(4)) multiplexer_3 (
    .in0(4'b0000), .in1(4'b0101), .out(multiplexer_3_out), .sel(STORE));  // open: en
  MAR mar_1 (.in_1(multiplexer_2_out), .in_2(or_3_out), .out_3(mar_1_out_3));
  not not_4 (not_4_out, register_4_q[6]);
  and and_5 (STORE, register_4_q[7], not_4_out);
  or or_3 (or_3_out, ONE, delay_4_out_2);
  and and_6 (and_6_out, FIVE, STORE);
  Register register_3 (.D(out_6), .Q(register_3_q), .clk(delay_3_out_2));  // open: en, clr
  DELAY delay_3 (.in_1(THREE), .out_2(delay_3_out_2));
  DELAY delay_4 (.in_1(and_6_out), .out_2(delay_4_out_2));
  Register register_4 (.D(register_3_q), .Q({register_4_q, ARG1, ARG2, address}), .clk(FOUR));  // open: en, clr
  Multiplexer #(.width(8)) multiplexer_4 (
    .in0(out_6), .in1(register_6_q), .out(multiplexer_4_out), .sel(_8));  // open: en
  DELAY delay_5 (.in_1(and_7_out), .out_2(delay_5_out_2));
  and and_7 (and_7_out, EGT, ADD, CLK);
  _8_bit_register u_8_bit_register_1 (.in_1(multiplexer_4_out), .in_2(and_8_out), .out_3(n8_bit_register_1_out_3));
  and and_8 (and_8_out, decoder_1_out0, delay_5_out_2, CLK);
  Decoder decoder_1 (.out0(decoder_1_out0), .out1(decoder_1_out1), .sel(and_9_out));  // open: en
  Clock clock_1 (.out(CLK));
  and and_9 (and_9_out, ARG1, ADD);
  Register register_5 (.D(multiplexer_4_out), .Q(register_5_q), .clk(and_10_out));  // open: en, clr
  and and_10 (and_10_out, decoder_1_out1, delay_5_out_2, CLK);
  and and_11 (and_11_out, ARG1, STORE);
  Multiplexer #(.width(8)) multiplexer_5 (
    .in0(n8_bit_register_1_out_3), .in1(register_5_q), .out(multiplexer_5_out), .sel(or_4_out));  // open: en
  or or_4 (or_4_out, and_11_out, and_12_out);
  and and_12 (and_12_out, or_5_out, ADD);
  or or_5 (or_5_out, and_13_out, and_15_out, and_14_out);
  and and_13 (and_13_out, FIVE, ARG1);
  and and_14 (and_14_out, SIX, ARG2);
  or or_6 (or_6_out, ADD, STORE);
  and and_15 (and_15_out, FOUR, ARG1);
  DELAY delay_6 (.in_1(and_16_out), .out_2(delay_6_out_2));
  Multiplexer #(.width(8)) multiplexer_6 (
    .in0(multiplexer_4_out), .in1(multiplexer_5_out), .out(multiplexer_6_out), .sel(or_6_out));  // open: en
  and and_16 (and_16_out, delay_7_out_2, FIVE);
  DELAY delay_7 (.in_1(CLK), .out_2(delay_7_out_2));
  _8_bit_register u_8_bit_register_2 (.in_1(multiplexer_6_out), .in_2(delay_6_out_2), .out_3(n8_bit_register_2_out_3));
  and and_17 (and_17_out, delay_8_out_2, SIX);
  DELAY delay_8 (.in_1(CLK), .out_2(delay_8_out_2));
  ADDER adder_3 (
    .in_1(in_2), .in_2(n8_bit_register_3_out_3), .in_3(n8_bit_register_2_out_3), .out_4(out_5),
    .out_5(adder_3_out_5));
  _8_bit_register u_8_bit_register_3 (.in_1(multiplexer_6_out), .in_2(delay_9_out_2), .out_3(n8_bit_register_3_out_3));
  DELAY delay_9 (.in_1(and_17_out), .out_2(delay_9_out_2));
  Register register_6 (.D(adder_3_out_5), .Q(register_6_q), .clk(and_18_out));  // open: en, clr
  and and_18 (and_18_out, CLK, SVN);
  T_Flip_Flop t_ff_1 (.clk(and_18_out), .T(or_6_out));  // open: Q, Qn, preset, reset, en
  // NOT_Gate not_5 is placed but not wired

  // Notes on the sheet:
  //   NOTE: ADD AND GATE IN TIMER
  //   IDEA: SEPARATE RAM INTO DATA AND INSTRUCTION FIELDS
  //   ITEM 4
  //   ITEM 1
  //   ITEM 3
  //   A-OUT
endmodule

module JMP (
  input  ITEM_2,
  input  [3:0] in_2,
  input  in_3,
  input  in_4,
  input  [3:0] in_5,
  input  in_6,
  input  [7:0] in_7,
  output [7:0] out_8,
  output [7:0] out_9,
  output out_10,
  output [7:0] out_11,
  output [7:0] out_12
);

  wire _0FLAG, _1, _2, _3, _6, _7, _8, ADD, and_1_out, and_2_out, and_3_out, and_5_out, and_7_out, and_8_out,
       and_10_out, and_12_out, and_14_out, and_15_out, and_16_out, and_17_out, and_18_out, and_19_out,
       and_20_out, and_21_out, and_22_out, and_23_out, and_24_out, and_25_out, ARG1, ARG2, BEQ, BNQ, CLK,
       decoder_1_out0, decoder_1_out1, delay_1_out_2, delay_2_out_2, delay_3_out_2, delay_4_out_2,
       delay_5_out_2, delay_6_out_2, delay_7_out_2, delay_8_out_2, delay_9_out_2, DONE, EGT, FIVE, FOUR,
       not_1_out, not_2_out, not_3_out, not_4_out, not_5_out, not_6_out, not_7_out, not_8_out, not_9_out,
       not_10_out, not_11_out, not_12_out, not_13_out, not_14_out, not_15_out, not_16_out, not_17_out,
       not_18_out, not_19_out, not_20_out, not_21_out, not_22_out, not_23_out, not_24_out, not_25_out,
       not_26_out, not_27_out, ONE, or_1_out, or_2_out, or_3_out, or_5_out, or_6_out, or_7_out, or_8_out,
       or_9_out, or_10_out, or_11_out, SIX, STOP, STORE, SVN, THREE, TWO, ZERO;
  wire [3:0] adder_1_out, address, main_1_p1, mar_1_out_3, multiplexer_1_out, multiplexer_2_out,
       multiplexer_3_out, multiplexer_4_out, multiplexer_5_out, or_4_out, register_1_q;
  wire [7:0] adder_3_out_5, multiplexer_6_out, multiplexer_7_out, multiplexer_8_out, n8_bit_register_1_out_3,
       register_2_q, register_3_q, register_5_q, register_6_q;
  wire [7:6] register_4_q;

  or or_1 (or_1_out, BEQ, BNQ);
  Adder #(.width(4)) adder_1 (.a(4'b0001), .b(register_1_q), .out(adder_1_out));  // open: cin, cout
  RAM ram_1 (.in_3(in_7), .in_1(in_3), .in_2(in_4), .out_5(out_11), .in_4(in_5));
  not not_1 (not_1_out, _1);
  not not_2 (not_2_out, _2);
  and and_1 (and_1_out, not_1_out, not_2_out, not_3_out);
  not not_3 (not_3_out, _2);
  Multiplexer #(.width(4)) multiplexer_1 (
    .in0(4'b0000), .in1(4'b0100), .out(multiplexer_1_out), .sel(or_3_out));  // open: en
  and and_2 (and_2_out, or_1_out, not_5_out);
  Multiplexer #(.width(4)) multiplexer_2 (
    .in0(adder_1_out), .in1(address), .out(multiplexer_2_out), .sel(and_2_out));  // open: en
  DELAY delay_1 (.in_1(or_2_out), .out_2(delay_1_out_2));
  or or_2 (or_2_out, TWO, and_3_out, and_5_out);
  and and_3 (and_3_out, not_4_out, EGT, BNQ);
  not not_4 (not_4_out, _0FLAG);
  and and_4 (BEQ, register_4_q[7], and_1_out, register_4_q[6]);
  or or_3 (or_3_out, BEQ, BNQ);
  not not_5 (not_5_out, ZERO);
  Register #(.width(4)) register_1 (.D(multiplexer_2_out), .Q(register_1_q), .clk(delay_1_out_2));  // open: en, clr
  and and_5 (and_5_out, _0FLAG, EGT, BEQ);
  not not_6 (not_6_out, register_4_q[7]);
  and and_6 (BNQ, not_6_out, and_1_out, register_4_q[6]);
  D_Flip_Flop d_ff_1 (.clk(FIVE), .D(STOP), .Q(DONE));  // open: Qn, preset, en, reset
  // _4BitCounter_main main_1: pin names not known; wires that end beside it: main_1_p1, DONE, _1, _2, _3, _6, _7
  assign or_4_out = multiplexer_5_out | multiplexer_1_out | multiplexer_3_out;  // OR_Gate or_4, 4 bits wide
  RAM ram_2 (.in_3(register_2_q), .in_1(and_7_out), .in_2(delay_2_out_2), .out_5(out_12), .in_4(mar_1_out_3));
  Multiplexer #(.width(4)) multiplexer_3 (
    .in0(4'b0000), .in1(4'b0100), .out(multiplexer_3_out), .sel(and_8_out));  // open: en
  not not_7 (not_7_out, STOP);
  Register register_2 (.D(multiplexer_8_out), .Q(register_2_q), .clk(SIX));  // open: en, clr
  Adder #(.width(4)) adder_2 (.a(4'b0100), .b(or_4_out), .out(main_1_p1));  // open: cin, cout
  or or_5 (or_5_out, _7, _8);
  and and_7 (and_7_out, STORE, or_5_out);
  DELAY delay_2 (.in_1(CLK), .out_2(delay_2_out_2));
  not not_8 (not_8_out, register_4_q[6]);
  not not_9 (not_9_out, register_4_q[7]);
  and and_8 (and_8_out, not_9_out, not_8_out);
  and and_9 (ADD, not_7_out, and_8_out);
  Multiplexer #(.width(4)) multiplexer_4 (
    .in0(register_1_q), .in1(address), .out(multiplexer_4_out), .sel(and_10_out));  // open: en
  and and_10 (and_10_out, STORE, not_10_out);
  not not_10 (not_10_out, ZERO);
  Multiplexer #(.width(4)) multiplexer_5 (
    .in0(4'b0000), .in1(4'b0101), .out(multiplexer_5_out), .sel(STORE));  // open: en
  MAR mar_1 (.in_1(multiplexer_4_out), .in_2(or_6_out), .out_3(mar_1_out_3));
  not not_11 (not_11_out, register_4_q[6]);
  and and_11 (STORE, register_4_q[7], not_11_out);
  or or_6 (or_6_out, ONE, delay_4_out_2);
  and and_12 (and_12_out, FIVE, STORE);
  Register register_3 (.D(out_12), .Q(register_3_q), .clk(delay_3_out_2));  // open: en, clr
  DELAY delay_3 (.in_1(THREE), .out_2(delay_3_out_2));
  not not_12 (not_12_out, address[0]);
  not not_13 (not_13_out, address[1]);
  DELAY delay_4 (.in_1(and_12_out), .out_2(delay_4_out_2));
  Register register_4 (.D(register_3_q), .Q({register_4_q, ARG1, ARG2, address}), .clk(FOUR));  // open: en, clr
  not not_14 (not_14_out, address[2]);
  not not_15 (not_15_out, address[3]);
  not not_16 (not_16_out, ARG2);
  not not_17 (not_17_out, ARG1);
  not not_18 (not_18_out, register_4_q[6]);
  not not_19 (not_19_out, register_4_q[7]);
  and and_13 (STOP, not_12_out, not_13_out, not_14_out, not_15_out, not_16_out, not_17_out, not_18_out, not_19_out);
  Multiplexer #(.width(8)) multiplexer_6 (
    .in0(out_12), .in1(register_6_q), .out(multiplexer_6_out), .sel(_8));  // open: en
  DELAY delay_5 (.in_1(and_14_out), .out_2(delay_5_out_2));
  and and_14 (and_14_out, EGT, ADD, CLK);
  _8_bit_register u_8_bit_register_1 (.in_1(multiplexer_6_out), .in_2(and_15_out), .out_3(n8_bit_register_1_out_3));
  and and_15 (and_15_out, decoder_1_out0, delay_5_out_2, CLK);
  Decoder decoder_1 (.out0(decoder_1_out0), .out1(decoder_1_out1), .sel(and_16_out));  // open: en
  Clock clock_1 (.out(CLK));
  and and_16 (and_16_out, ARG1, ADD);
  Register register_5 (.D(multiplexer_6_out), .Q(register_5_q), .clk(and_17_out));  // open: en, clr
  and and_17 (and_17_out, decoder_1_out1, delay_5_out_2, CLK);
  and and_18 (and_18_out, ARG1, STORE);
  Multiplexer #(.width(8)) multiplexer_7 (
    .in0(n8_bit_register_1_out_3), .in1(register_5_q), .out(multiplexer_7_out), .sel(or_7_out));  // open: en
  or or_7 (or_7_out, and_18_out, and_19_out);
  and and_19 (and_19_out, or_8_out, or_10_out);
  or or_8 (or_8_out, and_21_out, and_22_out, and_20_out);
  and and_20 (and_20_out, SIX, ARG2);
  and and_21 (and_21_out, FIVE, ARG1);
  or or_9 (or_9_out, ADD, or_10_out, STORE);
  and and_22 (and_22_out, FOUR, ARG1);
  DELAY delay_6 (.in_1(and_23_out), .out_2(delay_6_out_2));
  Multiplexer #(.width(8)) multiplexer_8 (
    .in0(multiplexer_6_out), .in1(multiplexer_7_out), .out(multiplexer_8_out), .sel(or_9_out));  // open: en
  and and_23 (and_23_out, delay_7_out_2, FIVE);
  DELAY delay_7 (.in_1(CLK), .out_2(delay_7_out_2));
  or or_10 (or_10_out, BEQ, ADD, BNQ);
  _8_bit_register u_8_bit_register_2 (.in_1(multiplexer_8_out), .in_2(delay_6_out_2), .out_3(out_9));
  and and_24 (and_24_out, delay_8_out_2, SIX);
  DELAY delay_8 (.in_1(CLK), .out_2(delay_8_out_2));
  ADDER adder_3 (.in_1(or_11_out), .in_2(out_8), .in_3(out_9), .out_4(out_10), .out_5(adder_3_out_5));
  _8_bit_register u_8_bit_register_3 (.in_1(multiplexer_8_out), .in_2(delay_9_out_2), .out_3(out_8));
  DELAY delay_9 (.in_1(and_24_out), .out_2(delay_9_out_2));
  or or_11 (or_11_out, BEQ, BNQ);
  Register register_6 (.D(adder_3_out_5), .Q(register_6_q), .clk(and_25_out));  // open: en, clr
  and and_25 (and_25_out, CLK, SVN);
  not not_20 (not_20_out, register_6_q[0]);
  not not_21 (not_21_out, register_6_q[1]);
  not not_22 (not_22_out, register_6_q[2]);
  not not_23 (not_23_out, register_6_q[5]);
  not not_24 (not_24_out, register_6_q[6]);
  not not_25 (not_25_out, register_6_q[7]);
  not not_26 (not_26_out, register_6_q[3]);
  not not_27 (not_27_out, register_6_q[4]);
  and and_26 (_0FLAG, not_20_out, not_21_out, not_22_out, not_26_out, not_27_out, not_23_out, not_24_out, not_25_out);
  // NOT_Gate not_28 is placed but not wired

  // Notes on the sheet:
  //   NOTE: ADD AND GATE IN TIMER
  //   AR
  //   IDEA: SEPARATE RAM INTO DATA AND INSTRUCTION FIELDS
  //   ITEM 4
  //   ITEM 1
  //   ITEM 3
  //   A-OUT
endmodule

module CONTROL_UNIT_2 (
  input  [7:0] in_1,
  input  in_2,
  output out_3,
  output out_4,
  output out_5,
  output out_6,
  output out_7,
  output out_8,
  output out_9,
  output out_10,
  output out_11,
  output out_12,
  output MUX_6,
  output out_14,
  output out_15,
  output out_16,
  output MAR,
  output out_18
);

  wire _00, _01, _1, _2, _3, _4, _5, _6, _7, _10, _11, ADD, ADD_out, and_9_out, and_11_out, and_12_out,
       and_13_out, and_15_out, ARG1, ARG2, BEQ, BNQ, delay_1_out_2, delay_2_out_2, delay_3_out_2,
       delay_4_out_2, delay_5_out_2, delay_6_out_2, delay_7_out_2, DEST, DONE, GO, INP_out, LOAD, not_1_out,
       not_2_out, not_3_out, not_4_out, not_5_out, not_6_out, not_7_out, not_8_out, not_9_out, not_10_out,
       not_11_out, not_12_out, not_13_out, not_14_out, not_15_out, not_16_out, not_17_out, not_18_out,
       not_19_out, not_20_out, not_21_out, or_1_out, or_2_out, or_5_out, or_6_out, or_10_out, PRT_out, STORE,
       STP, STP_out, SUB_out;
  wire [3:0] _1TK, _4TX, _5TX, adder_1_out, jmp, multiplexer_6_out, multiplexer_7_out, or_4_out;
  wire [7:0] multiplexer_3_out, multiplexer_5_out;

  D_Flip_Flop d_ff_1 (.clk(out_8), .D(STP), .Q(DONE));  // open: Qn, preset, en, reset
  not not_1 (not_1_out, multiplexer_5_out[2]);
  not not_2 (not_2_out, multiplexer_5_out[2]);
  not not_3 (not_3_out, multiplexer_5_out[3]);
  not not_4 (not_4_out, multiplexer_5_out[1]);
  not not_5 (not_5_out, multiplexer_5_out[1]);
  not not_6 (not_6_out, multiplexer_5_out[0]);
  and SUB (SUB_out, not_3_out, not_2_out, not_5_out, multiplexer_5_out[0]);
  and u_ADD (ADD_out, multiplexer_5_out[3], not_1_out, not_4_out, not_6_out);
  and and_1 (ADD, ADD_out, _00, GO);
  and and_2 (out_18, SUB_out, _00, GO);
  not not_7 (not_7_out, multiplexer_3_out[4]);
  and and_3 (LOAD, not_7_out, GO, _01);
  not not_8 (not_8_out, multiplexer_5_out[3]);
  not not_9 (not_9_out, multiplexer_5_out[3]);
  not not_10 (not_10_out, multiplexer_5_out[0]);
  and PRT (PRT_out, not_8_out, not_9_out, multiplexer_5_out[1], not_10_out);
  and and_4 (out_15, PRT_out, _00, GO);
  Multiplexer #(.width(4)) multiplexer_1 (.in0(4'b0000), .in1(4'b0100), .out(_4TX), .sel(or_1_out));  // open: en
  or or_1 (or_1_out, out_18, ADD);
  Multiplexer #(.width(4)) multiplexer_2 (.in0(4'b0000), .in1(4'b0010), .out(_1TK), .sel(or_2_out));  // open: en
  or or_2 (or_2_out, out_15, STP, out_16);
  and and_5 (STORE, multiplexer_3_out[4], GO, _01);
  not not_11 (not_11_out, multiplexer_5_out[3]);
  not not_12 (not_12_out, multiplexer_5_out[3]);
  not not_13 (not_13_out, multiplexer_5_out[2]);
  not not_14 (not_14_out, multiplexer_5_out[1]);
  not not_15 (not_15_out, multiplexer_5_out[0]);
  and u_STP (STP_out, not_12_out, not_13_out, not_14_out, not_15_out);
  and and_6 (STP, STP_out, _00, GO);
  Multiplexer #(.width(8)) multiplexer_3 (
    .in0({8{1'b0}}), .in1(in_1), .out({multiplexer_3_out[7:6], DEST, multiplexer_3_out[4:0]}), .sel(_01));  // open: en
  not not_16 (not_16_out, multiplexer_5_out[1]);
  not not_17 (not_17_out, multiplexer_5_out[0]);
  and INP (INP_out, not_11_out, multiplexer_5_out[2], not_16_out, not_17_out);
  and and_7 (out_16, INP_out, _00, GO);
  and and_8 (GO, not_18_out, and_9_out);
  Multiplexer #(.width(4)) multiplexer_4 (.in0(4'b0000), .in1(4'b0101), .out(_5TX), .sel(_01));  // open: en
  or or_3 (MUX_6, LOAD, STORE);
  not not_18 (not_18_out, out_3);
  not not_19 (not_19_out, _1);
  not not_20 (not_20_out, _2);
  and and_9 (and_9_out, not_19_out, not_20_out, not_21_out);
  not not_21 (not_21_out, _3);
  Multiplexer #(.width(8)) multiplexer_5 (
    .in0({8{1'b0}}), .in1(in_1), .out({multiplexer_5_out[7:6], ARG1, ARG2, multiplexer_5_out[3:0]}), .sel(_00));  // open: en
  assign or_4_out = _4TX | _1TK | jmp | _5TX;  // OR_Gate or_4, 4 bits wide
  // AND_Gate and_10 is placed but not wired
  Decoder #(.select(2)) decoder_1 (.out0(_00), .out1(_01), .out2(_10), .out3(_11), .sel(in_1[7:6]));  // open: en
  Adder #(.width(4)) adder_1 (.a(4'b0100), .b(or_4_out), .out(adder_1_out));  // open: cin, cout
  DELAY delay_1 (.in_1(and_11_out), .out_2(delay_1_out_2));
  and and_11 (and_11_out, or_5_out, out_8);
  buf or_5 (or_5_out, out_16);  // OR_Gate
  // _4BitCounter_main main_1: pin names not known; wires that end beside it: adder_1_out, DONE, _1, _2, _3, _4, _5, _6, _7
  or or_6 (or_6_out, delay_2_out_2, delay_1_out_2, and_12_out);
  and and_12 (and_12_out, delay_3_out_2, STORE);
  DELAY delay_2 (.in_1(out_6), .out_2(delay_2_out_2));
  DELAY delay_3 (.in_1(delay_4_out_2), .out_2(delay_3_out_2));
  DELAY delay_4 (.in_1(out_9), .out_2(delay_4_out_2));
  DELAY delay_5 (.in_1(delay_6_out_2), .out_2(delay_5_out_2));
  DELAY delay_6 (.in_1(out_10), .out_2(delay_6_out_2));
  or or_7 (out_14, or_6_out, and_13_out);
  and and_13 (and_13_out, delay_5_out_2, LOAD);
  assign jmp = multiplexer_6_out | multiplexer_7_out;  // OR_Gate or_8, 4 bits wide
  Multiplexer #(.width(4)) multiplexer_6 (
    .in0(4'b0000), .in1(4'b0101), .out(multiplexer_6_out), .sel(_10));  // open: en
  Multiplexer #(.width(4)) multiplexer_7 (
    .in0(4'b0000), .in1(4'b0101), .out(multiplexer_7_out), .sel(_11));  // open: en
  Multiplexer #(.width(8)) multiplexer_8 (.in0({8{1'b0}}), .in1(in_1), .sel(_10));  // open: out, en
  or or_9 (MAR, out_4, delay_7_out_2);
  and and_14 (BEQ, _10, GO);
  Multiplexer #(.width(8)) multiplexer_9 (.in0({8{1'b0}}), .in1(in_1), .sel(_11));  // open: out, en
  or or_10 (or_10_out, LOAD, STORE);
  and and_15 (and_15_out, out_8, or_10_out);
  DELAY delay_7 (.in_1(and_15_out), .out_2(delay_7_out_2));
  and and_16 (BNQ, _11, GO);
  // AND_Gate and_17 is placed but not wired

  // Other names for the same wires on the sheet: CLK = in_2; EGT = out_11; FIVE = out_8; FOUR = out_7; INP = out_16;
  //   INSTR[7:0] = in_1; NINE = out_12; ONE = out_4; PRT = out_15; SIX = out_9; SUB = out_18; SVN = out_10;
  //   THREE = out_6; TWO = out_5; ZERO = out_3

  // Notes on the sheet:
  //   ADDER PART
  //   MASTER_COUNTER
  //   MBR Clock
endmodule

module Keypad (
  input  in_1,
  input  in_2,
  input  in_3,
  input  in_4,
  input  in_5,
  input  in_6,
  input  in_7,
  input  in_8,
  input  in_9,
  input  in_10,
  output [7:0] out_11
);

  wire [7:0] multiplexer_1_out, multiplexer_2_out, multiplexer_3_out, multiplexer_4_out, multiplexer_5_out,
       multiplexer_6_out, multiplexer_7_out, multiplexer_8_out, multiplexer_9_out, multiplexer_10_out;

  Multiplexer #(.width(8)) multiplexer_1 (
    .in0({8{1'b0}}), .in1(8'h9), .out(multiplexer_1_out), .sel(in_9));  // open: en
  Multiplexer #(.width(8)) multiplexer_2 (
    .in0({8{1'b0}}), .in1(8'h8), .out(multiplexer_2_out), .sel(in_7));  // open: en
  Multiplexer #(.width(8)) multiplexer_3 (
    .in0({8{1'b0}}), .in1(8'h7), .out(multiplexer_3_out), .sel(in_10));  // open: en
  ExactlyOne xor_1[7:0] (
    .out(out_11), .in0(multiplexer_1_out), .in1(multiplexer_2_out), .in2(multiplexer_3_out),
    .in3(multiplexer_4_out), .in4(multiplexer_5_out), .in5(multiplexer_6_out), .in6(multiplexer_7_out),
    .in7(multiplexer_8_out), .in8(multiplexer_9_out), .in9(multiplexer_10_out));
  Multiplexer #(.width(8)) multiplexer_4 (
    .in0({8{1'b0}}), .in1(8'h6), .out(multiplexer_4_out), .sel(in_8));  // open: en
  Multiplexer #(.width(8)) multiplexer_5 (
    .in0({8{1'b0}}), .in1(8'h5), .out(multiplexer_5_out), .sel(in_5));  // open: en
  Multiplexer #(.width(8)) multiplexer_6 (
    .in0({8{1'b0}}), .in1(8'h4), .out(multiplexer_6_out), .sel(in_3));  // open: en
  Multiplexer #(.width(8)) multiplexer_7 (
    .in0({8{1'b0}}), .in1(8'h3), .out(multiplexer_7_out), .sel(in_6));  // open: en
  Multiplexer #(.width(8)) multiplexer_8 (
    .in0({8{1'b0}}), .in1(8'h2), .out(multiplexer_8_out), .sel(in_4));  // open: en
  Multiplexer #(.width(8)) multiplexer_9 (
    .in0({8{1'b0}}), .in1(8'h1), .out(multiplexer_9_out), .sel(in_2));  // open: en
  Multiplexer #(.width(8)) multiplexer_10 (
    .in0({8{1'b0}}), .in1({8{1'b0}}), .out(multiplexer_10_out), .sel(in_1));  // open: en
endmodule
