// Logisim project DDABBLE.circ as structural Verilog: 3 circuits, main circuit main
module main (
  input  in_1,
  input  in_2,
  input  in_3,
  input  in_4,
  input  in_5,
  input  in_6,
  input  in_7,
  input  in_8,
  input  in_9,
  input  in_10,
  input  in_11,
  input  in_12,
  input  in_13,
  input  in_14,
  input  in_15,
  input  in_16,
  input  in_17,
  input  in_18,
  input  in_19,
  input  in_20,
  output out_21,
  output out_22,
  output out_23,
  output out_24,
  output out_25,
  output out_26,
  output out_27,
  output out_28,
  output out_29,
  output out_30,
  output out_31,
  output out_32,
  output out_33,
  output out_34,
  output out_35,
  output out_36,
  output out_37,
  output out_38,
  output out_39,
  output out_40
);

  add_three add_three_1 (
    .in_1(in_1), .in_2(in_2), .in_3(in_3), .in_4(in_4), .out_5(out_23), .out_6(out_22), .out_7(out_21));  // open: out_8
  add_three add_three_2 (
    .in_1(in_5), .in_2(in_6), .in_3(in_7), .in_4(in_8), .out_5(out_27), .out_6(out_26), .out_7(out_25),
    .out_8(out_24));
  add_three add_three_3 (
    .in_1(in_9), .in_2(in_10), .in_3(in_11), .in_4(in_12), .out_5(out_31), .out_6(out_30), .out_7(out_29),
    .out_8(out_28));

  assign out_32 = in_13;
  assign out_33 = in_14;
  assign out_34 = in_15;
  assign out_35 = in_16;
  assign out_36 = in_17;
  assign out_37 = in_18;
  assign out_38 = in_19;
  assign out_39 = in_20;
  assign out_40 = 1'b0;
endmodule

module add_three (
  input  in_1,
  input  in_2,
  input  in_3,
  input  in_4,
  output out_5,
  output out_6,
  output out_7,
  output out_8
);

  wire adder_1_cout, and_1_out, and_2_out, not_1_out, not_2_out, or_1_out, or_2_out, or_3_out;
  wire [3:0] adder_1_out;

  or or_1 (or_1_out, in_2, in_3);
  not not_1 (not_1_out, or_1_out);
  or or_2 (or_2_out, in_3, in_4);
  and and_1 (and_1_out, in_2, or_2_out);
  and and_2 (and_2_out, in_1, not_1_out);
  or or_3 (or_3_out, and_1_out, and_2_out);
  not not_2 (not_2_out, or_3_out);
  Adder #(.width(4)) adder_1 (
    .a(4'b0011), .b({in_1, in_2, in_3, in_4}), .out(adder_1_out), .cin(1'b0), .cout(adder_1_cout));
  Multiplexer #(.width(4)) multiplexer_1 (
    .in0(adder_1_out), .in1({in_1, in_2, in_3, in_4}), .out({out_8, out_7, out_6, out_5}), .sel(not_2_out));  // open: en
endmodule

module Yeah (
  input  in_1,
  input  in_2,
  input  in_3,
  input  in_4,
  input  in_5,
  input  in_6,
  input  in_7,
  input  in_8,
  input  in_9,
  input  in_10,
  input  in_11,
  input  in_12,
  input  in_13,
  input  in_14,
  input  in_15,
  input  in_16,
  input  in_17,
  input  in_18,
  input  in_19,
  input  in_20,
  output [3:0] out_21,
  output [3:0] out_22,
  output [3:0] out_23
);

  wire main_1_out_21, main_1_out_22, main_1_out_23, main_1_out_24, main_1_out_25, main_1_out_26,
       main_1_out_27, main_1_out_28, main_1_out_29, main_1_out_30, main_1_out_31, main_1_out_32,
       main_1_out_33, main_1_out_34, main_1_out_35, main_1_out_36, main_1_out_37, main_1_out_38,
       main_1_out_39, main_1_out_40, main_2_out_21, main_2_out_22, main_2_out_23, main_2_out_24,
       main_2_out_25, main_2_out_26, main_2_out_27, main_2_out_28, main_2_out_29, main_2_out_30,
       main_2_out_31, main_2_out_32, main_2_out_33, main_2_out_34, main_2_out_35, main_2_out_36,
       main_2_out_37, main_2_out_38, main_2_out_39, main_2_out_40, main_3_out_21, main_3_out_22,
       main_3_out_23, main_3_out_24, main_3_out_25, main_3_out_26, main_3_out_27, main_3_out_28,
       main_3_out_29, main_3_out_30, main_3_out_31, main_3_out_32, main_3_out_33, main_3_out_34,
       main_3_out_35, main_3_out_36, main_3_out_37, main_3_out_38, main_3_out_39, main_3_out_40,
       main_4_out_21, main_4_out_22, main_4_out_23, main_4_out_24, main_4_out_25, main_4_out_26,
       main_4_out_27, main_4_out_28, main_4_out_29, main_4_out_30, main_4_out_31, main_4_out_32,
       main_4_out_33, main_4_out_34, main_4_out_35, main_4_out_36, main_4_out_37, main_4_out_38,
       main_4_out_39, main_4_out_40, main_5_out_21, main_5_out_22, main_5_out_23, main_5_out_24,
       main_5_out_25, main_5_out_26, main_5_out_27, main_5_out_28, main_5_out_29, main_5_out_30,
       main_5_out_31, main_5_out_32, main_5_out_33, main_5_out_34, main_5_out_35, main_5_out_36,
       main_5_out_37, main_5_out_38, main_5_out_39, main_5_out_40, main_6_out_21, main_6_out_22,
       main_6_out_23, main_6_out_24, main_6_out_25, main_6_out_26, main_6_out_27, main_6_out_28,
       main_6_out_29, main_6_out_30, main_6_out_31, main_6_out_32, main_6_out_33, main_6_out_34,
       main_6_out_35, main_6_out_36, main_6_out_37, main_6_out_38, main_6_out_39, main_6_out_40,
       main_7_out_21, main_7_out_22, main_7_out_23, main_7_out_24, main_7_out_25, main_7_out_26,
       main_7_out_27, main_7_out_28, main_7_out_29, main_7_out_30, main_7_out_31, main_7_out_32,
       main_7_out_33, main_7_out_34, main_7_out_35, main_7_out_36, main_7_out_37, main_7_out_38,
       main_7_out_39, main_7_out_40;

  main main_1 (
    .in_1(in_1), .in_2(in_2), .in_3(in_3), .in_4(in_4), .in_5(in_5), .in_6(in_6), .in_7(in_7), .in_8(in_8),
    .in_9(in_9), .in_10(in_10), .in_11(in_11), .in_12(in_12), .in_13(in_13), .in_14(in_14), .in_15(in_15),
    .in_16(in_16), .in_17(in_17), .in_18(in_18), .in_19(in_19), .in_20(in_20), .out_21(main_1_out_21),
    .out_22(main_1_out_22), .out_23(main_1_out_23), .out_24(main_1_out_24), .out_25(main_1_out_25),
    .out_26(main_1_out_26), .out_27(main_1_out_27), .out_28(main_1_out_28), .out_29(main_1_out_29),
    .out_30(main_1_out_30), .out_31(main_1_out_31), .out_32(main_1_out_32), .out_33(main_1_out_33),
    .out_34(main_1_out_34), .out_35(main_1_out_35), .out_36(main_1_out_36), .out_37(main_1_out_37),
    .out_38(main_1_out_38), .out_39(main_1_out_39), .out_40(main_1_out_40));
  main main_2 (
    .in_1(main_1_out_21), .in_2(main_1_out_22), .in_3(main_1_out_23), .in_4(main_1_out_24),
    .in_5(main_1_out_25), .in_6(main_1_out_26), .in_7(main_1_out_27), .in_8(main_1_out_28),
    .in_9(main_1_out_29), .in_10(main_1_out_30), .in_11(main_1_out_31), .in_12(main_1_out_32),
    .in_13(main_1_out_33), .in_14(main_1_out_34), .in_15(main_1_out_35), .in_16(main_1_out_36),
    .in_17(main_1_out_37), .in_18(main_1_out_38), .in_19(main_1_out_39), .in_20(main_1_out_40),
    .out_21(main_2_out_21), .out_22(main_2_out_22), .out_23(main_2_out_23), .out_24(main_2_out_24),
    .out_25(main_2_out_25), .out_26(main_2_out_26), .out_27(main_2_out_27), .out_28(main_2_out_28),
    .out_29(main_2_out_29), .out_30(main_2_out_30), .out_31(main_2_out_31), .out_32(main_2_out_32),
    .out_33(main_2_out_33), .out_34(main_2_out_34), .out_35(main_2_out_35), .out_36(main_2_out_36),
    .out_37(main_2_out_37), .out_38(main_2_out_38), .out_39(main_2_out_39), .out_40(main_2_out_40));
  main main_3 (
    .in_1(main_2_out_21), .in_2(main_2_out_22), .in_3(main_2_out_23), .in_4(main_2_out_24),
    .in_5(main_2_out_25), .in_6(main_2_out_26), .in_7(main_2_out_27), .in_8(main_2_out_28),
    .in_9(main_2_out_29), .in_10(main_2_out_30), .in_11(main_2_out_31), .in_12(main_2_out_32),
    .in_13(main_2_out_33), .in_14(main_2_out_34), .in_15(main_2_out_35), .in_16(main_2_out_36),
    .in_17(main_2_out_37), .in_18(main_2_out_38), .in_19(main_2_out_39), .in_20(main_2_out_40),
    .out_21(main_3_out_21), .out_22(main_3_out_22), .out_23(main_3_out_23), .out_24(main_3_out_24),
    .out_25(main_3_out_25), .out_26(main_3_out_26), .out_27(main_3_out_27), .out_28(main_3_out_28),
    .out_29(main_3_out_29), .out_30(main_3_out_30), .out_31(main_3_out_31), .out_32(main_3_out_32),
    .out_33(main_3_out_33), .out_34(main_3_out_34), .out_35(main_3_out_35), .out_36(main_3_out_36),
    .out_37(main_3_out_37), .out_38(main_3_out_38), .out_39(main_3_out_39), .out_40(main_3_out_40));
  main main_4 (
    .in_1(main_3_out_21), .in_2(main_3_out_22), .in_3(main_3_out_23), .in_4(main_3_out_24),
    .in_5(main_3_out_25), .in_6(main_3_out_26), .in_7(main_3_out_27), .in_8(main_3_out_28),
    .in_9(main_3_out_29), .in_10(main_3_out_30), .in_11(main_3_out_31), .in_12(main_3_out_32),
    .in_13(main_3_out_33), .in_14(main_3_out_34), .in_15(main_3_out_35), .in_16(main_3_out_36),
    .in_17(main_3_out_37), .in_18(main_3_out_38), .in_19(main_3_out_39), .in_20(main_3_out_40),
    .out_21(main_4_out_21), .out_22(main_4_out_22), .out_23(main_4_out_23), .out_24(main_4_out_24),
    .out_25(main_4_out_25), .out_26(main_4_out_26), .out_27(main_4_out_27), .out_28(main_4_out_28),
    .out_29(main_4_out_29), .out_30(main_4_out_30), .out_31(main_4_out_31), .out_32(main_4_out_32),
    .out_33(main_4_out_33), .out_34(main_4_out_34), .out_35(main_4_out_35), .out_36(main_4_out_36),
    .out_37(main_4_out_37), .out_38(main_4_out_38), .out_39(main_4_out_39), .out_40(main_4_out_40));
  main main_5 (
    .in_1(main_4_out_21), .in_2(main_4_out_22), .in_3(main_4_out_23), .in_4(main_4_out_24),
    .in_5(main_4_out_25), .in_6(main_4_out_26), .in_7(main_4_out_27), .in_8(main_4_out_28),
    .in_9(main_4_out_29), .in_10(main_4_out_30), .in_11(main_4_out_31), .in_12(main_4_out_32),
    .in_13(main_4_out_33), .in_14(main_4_out_34), .in_15(main_4_out_35), .in_16(main_4_out_36),
    .in_17(main_4_out_37), .in_18(main_4_out_38), .in_19(main_4_out_39), .in_20(main_4_out_40),
    .out_21(main_5_out_21), .out_22(main_5_out_22), .out_23(main_5_out_23), .out_24(main_5_out_24),
    .out_25(main_5_out_25), .out_26(main_5_out_26), .out_27(main_5_out_27), .out_28(main_5_out_28),
    .out_29(main_5_out_29), .out_30(main_5_out_30), .out_31(main_5_out_31), .out_32(main_5_out_32),
    .out_33(main_5_out_33), .out_34(main_5_out_34), .out_35(main_5_out_35), .out_36(main_5_out_36),
    .out_37(main_5_out_37), .out_38(main_5_out_38), .out_39(main_5_out_39), .out_40(main_5_out_40));
  main main_6 (
    .in_1(main_5_out_21), .in_2(main_5_out_22), .in_3(main_5_out_23), .in_4(main_5_out_24),
    .in_5(main_5_out_25), .in_6(main_5_out_26), .in_7(main_5_out_27), .in_8(main_5_out_28),
    .in_9(main_5_out_29), .in_10(main_5_out_30), .in_11(main_5_out_31), .in_12(main_5_out_32),
    .in_13(main_5_out_33), .in_14(main_5_out_34), .in_15(main_5_out_35), .in_16(main_5_out_36),
    .in_17(main_5_out_37), .in_18(main_5_out_38), .in_19(main_5_out_39), .in_20(main_5_out_40),
    .out_21(main_6_out_21), .out_22(main_6_out_22), .out_23(main_6_out_23), .out_24(main_6_out_24),
    .out_25(main_6_out_25), .out_26(main_6_out_26), .out_27(main_6_out_27), .out_28(main_6_out_28),
    .out_29(main_6_out_29), .out_30(main_6_out_30), .out_31(main_6_out_31), .out_32(main_6_out_32),
    .out_33(main_6_out_33), .out_34(main_6_out_34), .out_35(main_6_out_35), .out_36(main_6_out_36),
    .out_37(main_6_out_37), .out_38(main_6_out_38), .out_39(main_6_out_39), .out_40(main_6_out_40));
  main main_7 (
    .in_1(main_6_out_21), .in_2(main_6_out_22), .in_3(main_6_out_23), .in_4(main_6_out_24),
    .in_5(main_6_out_25), .in_6(main_6_out_26), .in_7(main_6_out_27), .in_8(main_6_out_28),
    .in_9(main_6_out_29), .in_10(main_6_out_30), .in_11(main_6_out_31), .in_12(main_6_out_32),
    .in_13(main_6_out_33), .in_14(main_6_out_34), .in_15(main_6_out_35), .in_16(main_6_out_36),
    .in_17(main_6_out_37), .in_18(main_6_out_38), .in_19(main_6_out_39), .in_20(main_6_out_40),
    .out_21(main_7_out_21), .out_22(main_7_out_22), .out_23(main_7_out_23), .out_24(main_7_out_24),
    .out_25(main_7_out_25), .out_26(main_7_out_26), .out_27(main_7_out_27), .out_28(main_7_out_28),
    .out_29(main_7_out_29), .out_30(main_7_out_30), .out_31(main_7_out_31), .out_32(main_7_out_32),
    .out_33(main_7_out_33), .out_34(main_7_out_34), .out_35(main_7_out_35), .out_36(main_7_out_36),
    .out_37(main_7_out_37), .out_38(main_7_out_38), .out_39(main_7_out_39), .out_40(main_7_out_40));
  main main_8 (
    .in_1(main_7_out_21), .in_2(main_7_out_22), .in_3(main_7_out_23), .in_4(main_7_out_24),
    .in_5(main_7_out_25), .in_6(main_7_out_26), .in_7(main_7_out_27), .in_8(main_7_out_28),
    .in_9(main_7_out_29), .in_10(main_7_out_30), .in_11(main_7_out_31), .in_12(main_7_out_32),
    .in_13(main_7_out_33), .in_14(main_7_out_34), .in_15(main_7_out_35), .in_16(main_7_out_36),
    .in_17(main_7_out_37), .in_18(main_7_out_38), .in_19(main_7_out_39), .in_20(main_7_out_40),
    .out_21(out_23[3]), .out_22(out_23[2]), .out_23(out_23[1]), .out_24(out_23[0]), .out_25(out_22[3]),
    .out_26(out_22[2]), .out_27(out_22[1]), .out_28(out_22[0]), .out_29(out_21[3]), .out_30(out_21[2]),
    .out_31(out_21[1]), .out_32(out_21[0]));  // open: out_33, out_34, out_35, out_36, out_37, out_38, out_39, out_40
endmodule
