// Logisim project MINIRAM-updated.circ as structural Verilog: 6 circuits, main circuit BYTE
module BYTE (
  input  [1:0] in_1,
  input  in_2,
  input  [7:0] in_3,
  output [7:0] out_4
);

  wire and_1_out;

  and and_1 (and_1_out, in_1[1], in_1[0], in_2);
  D_Flip_Flop d_ff_1 (.clk(and_1_out), .D(in_3[7]), .Q(out_4[7]));  // open: Qn, preset, en, reset
  D_Flip_Flop d_ff_2 (.clk(and_1_out), .D(in_3[6]), .Q(out_4[6]));  // open: Qn, preset, en, reset
  D_Flip_Flop d_ff_3 (.clk(and_1_out), .D(in_3[5]), .Q(out_4[5]));  // open: Qn, preset, en, reset
  D_Flip_Flop d_ff_4 (.clk(and_1_out), .D(in_3[4]), .Q(out_4[4]));  // open: Qn, preset, en, reset
  D_Flip_Flop d_ff_5 (.clk(and_1_out), .D(in_3[3]), .Q(out_4[3]));  // open: Qn, preset, en, reset
  D_Flip_Flop d_ff_6 (.clk(and_1_out), .D(in_3[2]), .Q(out_4[2]));  // open: Qn, preset, en, reset
  D_Flip_Flop d_ff_7 (.clk(and_1_out), .D(in_3[1]), .Q(out_4[1]));  // open: Qn, preset, en, reset
  D_Flip_Flop d_ff_8 (.clk(and_1_out), .D(in_3[0]), .Q(out_4[0]));  // open: Qn, preset, en, reset
endmodule

module _16BYTERAM (
  input  [3:0] in_1,
  input  [7:0] in_2,
  input  [7:0] in_3,
  output [7:0] out_4
);

  wire data_register_1_p4;
  wire [1:0] decoder_1_out0, decoder_1_out1, decoder_1_out2, decoder_1_out3, decoder_1_out4, decoder_1_out5,
       decoder_1_out6, decoder_1_out7, decoder_1_out8, decoder_1_out9, decoder_1_out10, decoder_1_out11,
       decoder_1_out12, decoder_1_out13, decoder_1_out14, decoder_1_out15;
  wire [7:0] byte_1_out_4, byte_2_out_4, byte_3_out_4, byte_4_out_4, byte_5_out_4, byte_6_out_4,
       byte_7_out_4, byte_8_out_4, byte_9_out_4, byte_10_out_4, byte_11_out_4, byte_12_out_4, byte_13_out_4,
       byte_14_out_4, byte_15_out_4, byte_16_out_4, data_register_1_p1, or_1_out, or_2_out;

  assign or_1_out = byte_1_out_4 | byte_5_out_4 | byte_6_out_4 | byte_3_out_4 | byte_7_out_4 | byte_4_out_4 | byte_8_out_4 | byte_2_out_4;  // OR_Gate or_1, 8 bits wide
  BYTE byte_1 (.in_3(in_3), .in_1(decoder_1_out0), .in_2(data_register_1_p4), .out_4(byte_1_out_4));
  BYTE byte_2 (.in_3(in_3), .in_1(decoder_1_out2), .in_2(data_register_1_p4), .out_4(byte_2_out_4));
  BYTE byte_3 (.in_3(in_3), .in_1(decoder_1_out4), .in_2(data_register_1_p4), .out_4(byte_3_out_4));
  BYTE byte_4 (.in_3(in_3), .in_1(decoder_1_out6), .in_2(data_register_1_p4), .out_4(byte_4_out_4));
  BYTE byte_5 (.in_3(in_3), .in_1(decoder_1_out1), .in_2(data_register_1_p4), .out_4(byte_5_out_4));
  BYTE byte_6 (.in_3(in_3), .in_1(decoder_1_out3), .in_2(data_register_1_p4), .out_4(byte_6_out_4));
  BYTE byte_7 (.in_3(in_3), .in_1(decoder_1_out5), .in_2(data_register_1_p4), .out_4(byte_7_out_4));
  BYTE byte_8 (.in_3(in_3), .in_1(decoder_1_out7), .in_2(data_register_1_p4), .out_4(byte_8_out_4));
  Decoder #(.select(4)) decoder_1 (
    .out0(decoder_1_out0[0]), .out1(decoder_1_out1[0]), .out2(decoder_1_out2[0]), .out3(decoder_1_out3[0]),
    .out4(decoder_1_out4[0]), .out5(decoder_1_out5[0]), .out6(decoder_1_out6[0]), .out7(decoder_1_out7[0]),
    .out8(decoder_1_out8[0]), .out9(decoder_1_out9[0]), .out10(decoder_1_out10[0]),
    .out11(decoder_1_out11[0]), .out12(decoder_1_out12[0]), .out13(decoder_1_out13[0]),
    .out14(decoder_1_out14[0]), .out15(decoder_1_out15[0]), .sel(in_1));  // open: en
  BYTE byte_9 (.in_3(in_3), .in_1(decoder_1_out15), .in_2(data_register_1_p4), .out_4(byte_9_out_4));
  BYTE byte_10 (.in_3(in_3), .in_1(decoder_1_out13), .in_2(data_register_1_p4), .out_4(byte_10_out_4));
  BYTE byte_11 (.in_3(in_3), .in_1(decoder_1_out11), .in_2(data_register_1_p4), .out_4(byte_11_out_4));
  BYTE byte_12 (.in_3(in_3), .in_1(decoder_1_out9), .in_2(data_register_1_p4), .out_4(byte_12_out_4));
  BYTE byte_13 (.in_3(in_3), .in_1(decoder_1_out14), .in_2(data_register_1_p4), .out_4(byte_13_out_4));
  BYTE byte_14 (.in_3(in_3), .in_1(decoder_1_out12), .in_2(data_register_1_p4), .out_4(byte_14_out_4));
  BYTE byte_15 (.in_3(in_3), .in_1(decoder_1_out10), .in_2(data_register_1_p4), .out_4(byte_15_out_4));
  BYTE byte_16 (.in_3(in_3), .in_1(decoder_1_out8), .in_2(data_register_1_p4), .out_4(byte_16_out_4));
  // Data_Register data_register_1: pin names not known; wires that end beside it: data_register_1_p1, in_2, out_4, data_register_1_p4
  assign or_2_out = byte_16_out_4 | byte_12_out_4 | byte_15_out_4 | byte_11_out_4 | byte_14_out_4 | byte_10_out_4 | byte_13_out_4 | byte_9_out_4;  // OR_Gate or_2, 8 bits wide
  assign data_register_1_p1 = or_2_out | or_1_out;  // OR_Gate or_3, 8 bits wide
  // Pins of 1 and 2 bits meet at decoder_1_out15
  // Pins of 1 and 2 bits meet at decoder_1_out12
  // Pins of 1 and 2 bits meet at decoder_1_out0
  // Pins of 1 and 2 bits meet at decoder_1_out14
  // Pins of 1 and 2 bits meet at decoder_1_out13
  // Pins of 1 and 2 bits meet at decoder_1_out1
  // Pins of 1 and 2 bits meet at decoder_1_out2
  // Pins of 1 and 2 bits meet at decoder_1_out3
  // Pins of 1 and 2 bits meet at decoder_1_out4
  // Pins of 1 and 2 bits meet at decoder_1_out5
  // Pins of 1 and 2 bits meet at decoder_1_out6
  // Pins of 1 and 2 bits meet at decoder_1_out7
endmodule

module cck (
);

  wire demultiplexer_1_out0, demultiplexer_1_out1, undriven;
  wire [7:0] multiplexer_1_out, undriven_2, undriven_3;

  Multiplexer #(.width(8)) multiplexer_1 (
    .in0(undriven_2), .in1(undriven_3), .out(multiplexer_1_out));  // open: sel, en
  Demultiplexer demultiplexer_1 (
    .out0(demultiplexer_1_out0), .out1(demultiplexer_1_out1), .in(undriven));  // open: sel, en
endmodule

module Data_Register (
  input  [7:0] in_1,
  input  [7:0] in_2,
  input  in_3,
  input  in_4,
  output [1:0] out_5,
  output [7:0] out_6,
  output [7:0] out_7
);

  wire and_1_out, and_2_out, and_3_out, and_4_out, and_5_out, and_6_out, and_7_out, and_8_out, and_9_out,
       and_10_out, and_11_out, and_12_out, and_13_out, and_14_out, and_15_out;
  wire [7:0] d_ff_8_q, multiplexer_1_out;

  Multiplexer #(.width(8)) multiplexer_1 (.in0(in_1), .in1(in_2), .out(multiplexer_1_out), .sel(in_3));  // open: en
  D_Flip_Flop d_ff_1 (.clk(out_5[0]), .D(multiplexer_1_out[7]), .Q(d_ff_8_q[7]));  // open: Qn, preset, en, reset
  and and_1 (and_1_out, in_4, in_4);
  D_Flip_Flop d_ff_2 (.clk(out_5[0]), .D(multiplexer_1_out[6]), .Q(d_ff_8_q[6]));  // open: Qn, preset, en, reset
  and and_2 (and_2_out, and_1_out, and_1_out);
  D_Flip_Flop d_ff_3 (.clk(out_5[0]), .D(multiplexer_1_out[5]), .Q(d_ff_8_q[5]));  // open: Qn, preset, en, reset
  and and_3 (and_3_out, and_2_out, and_2_out);
  and and_4 (and_4_out, and_3_out, and_3_out);
  and and_5 (and_5_out, and_4_out, and_4_out);
  D_Flip_Flop d_ff_4 (.clk(out_5[0]), .D(multiplexer_1_out[4]), .Q(d_ff_8_q[4]));  // open: Qn, preset, en, reset
  and and_6 (and_6_out, and_5_out, and_5_out);
  and and_7 (and_7_out, and_6_out, and_6_out);
  D_Flip_Flop d_ff_5 (.clk(out_5[0]), .D(multiplexer_1_out[3]), .Q(d_ff_8_q[3]));  // open: Qn, preset, en, reset
  and and_8 (and_8_out, and_9_out, and_9_out);
  and and_9 (and_9_out, and_7_out, and_7_out);
  D_Flip_Flop d_ff_6 (.clk(out_5[0]), .D(multiplexer_1_out[2]), .Q(d_ff_8_q[2]));  // open: Qn, preset, en, reset
  Demultiplexer #(.width(8)) demultiplexer_1 (.out0(out_6), .out1(out_7), .in(d_ff_8_q), .sel(in_3));  // open: en
  and and_10 (and_10_out, and_8_out, and_8_out);
  D_Flip_Flop d_ff_7 (.clk(out_5[0]), .D(multiplexer_1_out[1]), .Q(d_ff_8_q[1]));  // open: Qn, preset, en, reset
  and and_11 (and_11_out, and_12_out, and_12_out);
  and and_12 (and_12_out, and_10_out, and_10_out);
  D_Flip_Flop d_ff_8 (.clk(out_5[0]), .D(multiplexer_1_out[0]), .Q(d_ff_8_q[0]));  // open: Qn, preset, en, reset
  and and_13 (and_13_out, and_11_out, and_11_out);
  and and_14 (and_14_out, and_13_out, and_13_out);
  and and_15 (and_15_out, and_14_out, and_14_out);
  and and_16 (out_5[0], and_15_out, and_15_out);

  assign out_5[1] = in_3;
endmodule

module RAM (
  input  in_1,
  input  in_2,
  input  [7:0] in_3,
  input  [3:0] in_4,
  output out_5,
  output [7:0] out_6
);

  wire decoder_1_out0, decoder_1_out1, decoder_1_out2, decoder_1_out3, decoder_1_out4, decoder_1_out5,
       decoder_1_out6, decoder_1_out7, decoder_1_out8, decoder_1_out9, decoder_1_out10, decoder_1_out11,
       decoder_1_out12, decoder_1_out13, decoder_1_out14, decoder_1_out15;
  wire [1:0] data_register_1_out_5;
  wire [3:0] n4_bit_register_1_out_3;
  wire [7:0] byte_1_out_4, byte_2_out_4, byte_3_out_4, byte_4_out_4, byte_5_out_4, byte_6_out_4,
       byte_7_out_4, byte_8_out_4, byte_9_out_4, byte_10_out_4, byte_11_out_4, byte_12_out_4, byte_13_out_4,
       byte_14_out_4, byte_15_out_4, byte_16_out_4, data_register_1_out_7, multiplexer_1_out;

  BYTE byte_1 (.in_3(data_register_1_out_7), .in_1(data_register_1_out_5), .in_2(decoder_1_out0), .out_4(byte_1_out_4));
  BYTE byte_2 (.in_3(data_register_1_out_7), .in_1(data_register_1_out_5), .in_2(decoder_1_out2), .out_4(byte_2_out_4));
  BYTE byte_3 (.in_3(data_register_1_out_7), .in_1(data_register_1_out_5), .in_2(decoder_1_out4), .out_4(byte_3_out_4));
  BYTE byte_4 (.in_3(data_register_1_out_7), .in_1(data_register_1_out_5), .in_2(decoder_1_out6), .out_4(byte_4_out_4));
  BYTE byte_5 (.in_3(data_register_1_out_7), .in_1(data_register_1_out_5), .in_2(decoder_1_out1), .out_4(byte_5_out_4));
  BYTE byte_6 (.in_3(data_register_1_out_7), .in_1(data_register_1_out_5), .in_2(decoder_1_out3), .out_4(byte_6_out_4));
  BYTE byte_7 (.in_3(data_register_1_out_7), .in_1(data_register_1_out_5), .in_2(decoder_1_out5), .out_4(byte_7_out_4));
  BYTE byte_8 (.in_3(data_register_1_out_7), .in_1(data_register_1_out_5), .in_2(decoder_1_out7), .out_4(byte_8_out_4));
  Decoder #(.select(4)) decoder_1 (
    .out0(decoder_1_out0), .out1(decoder_1_out1), .out2(decoder_1_out2), .out3(decoder_1_out3),
    .out4(decoder_1_out4), .out5(decoder_1_out5), .out6(decoder_1_out6), .out7(decoder_1_out7),
    .out8(decoder_1_out8), .out9(decoder_1_out9), .out10(decoder_1_out10), .out11(decoder_1_out11),
    .out12(decoder_1_out12), .out13(decoder_1_out13), .out14(decoder_1_out14), .out15(decoder_1_out15),
    .sel(n4_bit_register_1_out_3));  // open: en
  Multiplexer #(.select(4), .width(8)) multiplexer_1 (
    .in0(byte_1_out_4), .in1(byte_5_out_4), .in2(byte_2_out_4), .in3(byte_6_out_4), .in4(byte_3_out_4),
    .in5(byte_7_out_4), .in6(byte_4_out_4), .in7(byte_8_out_4), .in8(byte_16_out_4), .in9(byte_12_out_4),
    .in10(byte_15_out_4), .in11(byte_11_out_4), .in12(byte_14_out_4), .in13(byte_10_out_4),
    .in14(byte_13_out_4), .in15(byte_9_out_4), .out(multiplexer_1_out), .sel(n4_bit_register_1_out_3));  // open: en
  BYTE byte_9 (
    .in_3(data_register_1_out_7), .in_1(data_register_1_out_5), .in_2(decoder_1_out15), .out_4(byte_9_out_4));
  BYTE byte_10 (
    .in_3(data_register_1_out_7), .in_1(data_register_1_out_5), .in_2(decoder_1_out13), .out_4(byte_10_out_4));
  BYTE byte_11 (
    .in_3(data_register_1_out_7), .in_1(data_register_1_out_5), .in_2(decoder_1_out11), .out_4(byte_11_out_4));
  BYTE byte_12 (
    .in_3(data_register_1_out_7), .in_1(data_register_1_out_5), .in_2(decoder_1_out9), .out_4(byte_12_out_4));
  _4_bit_Register u_4_bit_register_1 (.in_1(in_2), .in_2(in_4), .out_3(n4_bit_register_1_out_3));
  BYTE byte_13 (
    .in_3(data_register_1_out_7), .in_1(data_register_1_out_5), .in_2(decoder_1_out14), .out_4(byte_13_out_4));
  BYTE byte_14 (
    .in_3(data_register_1_out_7), .in_1(data_register_1_out_5), .in_2(decoder_1_out12), .out_4(byte_14_out_4));
  BYTE byte_15 (
    .in_3(data_register_1_out_7), .in_1(data_register_1_out_5), .in_2(decoder_1_out10), .out_4(byte_15_out_4));
  BYTE byte_16 (
    .in_3(data_register_1_out_7), .in_1(data_register_1_out_5), .in_2(decoder_1_out8), .out_4(byte_16_out_4));
  Data_Register data_register_1 (
    .in_1(multiplexer_1_out), .in_2(in_3), .in_3(in_1), .in_4(in_2), .out_5(data_register_1_out_5),
    .out_6(out_6), .out_7(data_register_1_out_7));
  or or_1 (out_5, n4_bit_register_1_out_3[3], n4_bit_register_1_out_3[2], n4_bit_register_1_out_3[1], n4_bit_register_1_out_3[0]);
endmodule

module _4_bit_Register (
  input  in_1,
  input  [3:0] in_2,
  output [3:0] out_3
);

  D_Flip_Flop d_ff_1 (.clk(in_1), .D(in_2[0]), .Q(out_3[0]));  // open: Qn, preset, en, reset
  D_Flip_Flop d_ff_2 (.clk(in_1), .D(in_2[1]), .Q(out_3[1]));  // open: Qn, preset, en, reset
  D_Flip_Flop d_ff_3 (.clk(in_1), .D(in_2[2]), .Q(out_3[2]));  // open: Qn, preset, en, reset
  D_Flip_Flop d_ff_4 (.clk(in_1), .D(in_2[3]), .Q(out_3[3]));  // open: Qn, preset, en, reset
endmodule
