// Logisim project display.circ as structural Verilog: 1 circuit, main circuit main
module main (
  input  [3:0] in_1,
  output out_2,
  output out_3,
  output out_4,
  output out_5,
  output out_6,
  output out_7,
  output out_8
);

  wire decoder_1_out0, decoder_1_out1, decoder_1_out2, decoder_1_out3, decoder_1_out4, decoder_1_out5,
       decoder_1_out6, decoder_1_out7, decoder_1_out8, decoder_1_out9;

  Multiplexer #(.select(4)) multiplexer_1 (
    .in0(decoder_1_out0), .in1(decoder_1_out1), .in2(decoder_1_out2), .in3(decoder_1_out3),
    .in4(decoder_1_out4), .in7(decoder_1_out7), .in8(decoder_1_out8), .in9(decoder_1_out9), .out(out_5),
    .sel(in_1));  // open: in5, in6, in10, in11, in12, in13, in14, in15, en
  Multiplexer #(.select(4)) multiplexer_2 (
    .in0(decoder_1_out0), .in2(decoder_1_out2), .in3(decoder_1_out3), .in5(decoder_1_out5),
    .in6(decoder_1_out6), .in7(decoder_1_out7), .in8(decoder_1_out8), .in9(decoder_1_out9), .out(out_4),
    .sel(in_1));  // open: in1, in4, in10, in11, in12, in13, in14, in15, en
  _7_Segment_Display u_7_segment_display_1 (
    .g(out_2), .f(out_3), .a(out_4), .b(out_5), .e(out_8), .d(out_7), .c(out_6));  // open: dp
  Multiplexer #(.select(4)) multiplexer_3 (
    .in0(decoder_1_out0), .in4(decoder_1_out4), .in5(decoder_1_out5), .in6(decoder_1_out6),
    .in8(decoder_1_out8), .in9(decoder_1_out9), .out(out_3), .sel(in_1));  // open: in1, in2, in3, in7, in10, in11, in12, in13, in14, in15, en
  Decoder #(.select(4)) decoder_1 (
    .out0(decoder_1_out0), .out1(decoder_1_out1), .out2(decoder_1_out2), .out3(decoder_1_out3),
    .out4(decoder_1_out4), .out5(decoder_1_out5), .out6(decoder_1_out6), .out7(decoder_1_out7),
    .out8(decoder_1_out8), .out9(decoder_1_out9), .sel(in_1));  // open: out10, out11, out12, out13, out14, out15, en
  Multiplexer #(.select(4)) multiplexer_4 (
    .in2(decoder_1_out2), .in3(decoder_1_out3), .in4(decoder_1_out4), .in5(decoder_1_out5),
    .in6(decoder_1_out6), .in8(decoder_1_out8), .in9(decoder_1_out9), .out(out_2), .sel(in_1));  // open: in0, in1, in7, in10, in11, in12, in13, in14, in15, en
  Multiplexer #(.select(4)) multiplexer_5 (
    .in0(decoder_1_out0), .in2(decoder_1_out2), .in6(decoder_1_out6), .in8(decoder_1_out8), .out(out_8),
    .sel(in_1));  // open: in1, in3, in4, in5, in7, in9, in10, in11, in12, in13, in14, in15, en
  Multiplexer #(.select(4)) multiplexer_6 (
    .in0(decoder_1_out0), .in2(decoder_1_out2), .in3(decoder_1_out3), .in5(decoder_1_out5),
    .in6(decoder_1_out6), .in8(decoder_1_out8), .in9(decoder_1_out9), .out(out_7), .sel(in_1));  // open: in1, in4, in7, in10, in11, in12, in13, in14, in15, en
  Multiplexer #(.select(4)) multiplexer_7 (
    .in0(decoder_1_out0), .in1(decoder_1_out1), .in3(decoder_1_out3), .in4(decoder_1_out4),
    .in5(decoder_1_out5), .in6(decoder_1_out6), .in7(decoder_1_out7), .in8(decoder_1_out8),
    .in9(decoder_1_out9), .out(out_6), .sel(in_1));  // open: in2, in10, in11, in12, in13, in14, in15, en

  // Notes on the sheet:
  //   right upper corner 
  //   input selection 
  //   top
  //   left upper corner 
  //   center
  //   lower left corner
  //   bottom
  //   lower right corner
endmodule
